// Digital circuit 16BitBSD.dig as structural Verilog
module _16BitBSD (
  input  [31:0] inA,
  input  [31:0] inB,
  output [31:0] out,
  output [1:0] carry
);

  wire add_1_c_o, add_1_s, add_2_c_o, add_2_s, add_3_c_o, add_3_s, add_4_c_o, add_4_s, add_5_c_o, add_5_s,
       add_6_c_o, add_6_s, add_7_c_o, add_7_s, add_8_s, add_9_c_o, add_9_s, add_10_c_o, add_10_s, add_11_c_o,
       add_11_s, add_12_c_o, add_12_s, add_13_c_o, add_13_s, add_14_c_o, add_14_s, add_15_c_o, add_15_s,
       add_16_c_o, add_16_s;

  Add add_1 (.a(inA[16]), .b(inB[16]), .c_i(inA[17]), .s(add_1_s), .c_o(add_1_c_o));
  Add add_2 (.a(inA[18]), .b(inB[18]), .c_i(inA[19]), .s(add_2_s), .c_o(add_2_c_o));
  Add add_3 (.a(inA[20]), .b(inB[20]), .c_i(inA[21]), .s(add_3_s), .c_o(add_3_c_o));
  Add add_4 (.a(inA[22]), .b(inB[22]), .c_i(inA[23]), .s(add_4_s), .c_o(add_4_c_o));
  Add add_5 (.a(inA[24]), .b(inB[24]), .c_i(inA[25]), .s(add_5_s), .c_o(add_5_c_o));
  Add add_6 (.a(inA[26]), .b(inB[26]), .c_i(inA[27]), .s(add_6_s), .c_o(add_6_c_o));
  Add add_7 (.a(inA[28]), .b(inB[28]), .c_i(inA[29]), .s(add_7_s), .c_o(add_7_c_o));
  Add add_8 (.a(inA[30]), .b(inB[30]), .c_i(inA[31]), .s(add_8_s), .c_o(carry[1]));
  Add add_9 (.a(inA[0]), .b(inB[0]), .c_i(inA[1]), .s(add_9_s), .c_o(add_9_c_o));
  Add add_10 (.a(inA[2]), .b(inB[2]), .c_i(inA[3]), .s(add_10_s), .c_o(add_10_c_o));
  Add add_11 (.a(inA[4]), .b(inB[4]), .c_i(inA[5]), .s(add_11_s), .c_o(add_11_c_o));
  Add add_12 (.a(inA[6]), .b(inB[6]), .c_i(inA[7]), .s(add_12_s), .c_o(add_12_c_o));
  Add add_13 (.a(inA[8]), .b(inB[8]), .c_i(inA[9]), .s(add_13_s), .c_o(add_13_c_o));
  Add add_14 (.a(inA[10]), .b(inB[10]), .c_i(inA[11]), .s(add_14_s), .c_o(add_14_c_o));
  Add add_15 (.a(inA[12]), .b(inB[12]), .c_i(inA[13]), .s(add_15_s), .c_o(add_15_c_o));
  Add add_16 (.a(inA[14]), .b(inB[14]), .c_i(inA[15]), .s(add_16_s), .c_o(add_16_c_o));
  Add add_17 (.a(1'b1), .b(add_9_s), .c_i(inB[1]), .s(out[1]), .c_o(out[2]));
  Add add_18 (.a(add_9_c_o), .b(add_10_s), .c_i(inB[3]), .s(out[3]), .c_o(out[4]));
  Add add_19 (.a(add_10_c_o), .b(add_11_s), .c_i(inB[5]), .s(out[5]), .c_o(out[6]));
  Add add_20 (.a(add_11_c_o), .b(add_12_s), .c_i(inB[7]), .s(out[7]), .c_o(out[8]));
  Add add_21 (.a(add_12_c_o), .b(add_13_s), .c_i(inB[9]), .s(out[9]), .c_o(out[10]));
  Add add_22 (.a(add_13_c_o), .b(add_14_s), .c_i(inB[11]), .s(out[11]), .c_o(out[12]));
  Add add_23 (.a(add_14_c_o), .b(add_15_s), .c_i(inB[13]), .s(out[13]), .c_o(out[14]));
  Add add_24 (.a(add_15_c_o), .b(add_16_s), .c_i(inB[15]), .s(out[15]), .c_o(out[16]));
  Add add_25 (.a(add_16_c_o), .b(add_1_s), .c_i(inB[17]), .s(out[17]), .c_o(out[18]));
  Add add_26 (.a(add_1_c_o), .b(add_2_s), .c_i(inB[19]), .s(out[19]), .c_o(out[20]));
  Add add_27 (.a(add_2_c_o), .b(add_3_s), .c_i(inB[21]), .s(out[21]), .c_o(out[22]));
  Add add_28 (.a(add_3_c_o), .b(add_4_s), .c_i(inB[23]), .s(out[23]), .c_o(out[24]));
  Add add_29 (.a(add_4_c_o), .b(add_5_s), .c_i(inB[25]), .s(out[25]), .c_o(out[26]));
  Add add_30 (.a(add_5_c_o), .b(add_6_s), .c_i(inB[27]), .s(out[27]), .c_o(out[28]));
  Add add_31 (.a(add_6_c_o), .b(add_7_s), .c_i(inB[29]), .s(out[29]), .c_o(out[30]));
  Add add_32 (.a(add_7_c_o), .b(add_8_s), .c_i(inB[31]), .s(out[31]), .c_o(carry[0]));

  assign out[0] = 1'b0;

  // Other names for the same wires on the sheet: _1 = inA[0]; _2 = inA[1]; _3 = inA[2]; _4 = inA[3]; _5 = inA[4];
  //   _6 = inA[5]; _7 = inA[6]; _8 = inA[7]; _9 = inA[8]; _10 = inA[9]; _11 = inA[10]; _12 = inA[11]; _13 = inA[12];
  //   _14 = inA[13]; _15 = inA[14]; _16 = inA[15]; _1c = inA[16]; _2c = inA[17]; _3c = inA[18]; _4c = inA[19];
  //   _5c = inA[20]; _6c = inA[21]; _7c = inA[22]; _8c = inA[23]; _9c = inA[24]; _10c = inA[25]; _11c = inA[26];
  //   _12c = inA[27]; _13c = inA[28]; _14c = inA[29]; _15c = inA[30]; _16c = inA[31]; _1b = inB[0]; _2b = inB[1];
  //   _3b = inB[2]; _4b = inB[3]; _5b = inB[4]; _6b = inB[5]; _7b = inB[6]; _8b = inB[7]; _9b = inB[8]; _10b = inB[9];
  //   _11b = inB[10]; _12b = inB[11]; _13b = inB[12]; _14b = inB[13]; _15b = inB[14]; _16b = inB[15]; _1bc = inB[16];
  //   _2bc = inB[17]; _3bc = inB[18]; _4bc = inB[19]; _5bc = inB[20]; _6bc = inB[21]; _7bc = inB[22]; _8bc = inB[23];
  //   _9bc = inB[24]; _10bc = inB[25]; _11bc = inB[26]; _12bc = inB[27]; _13bc = inB[28]; _14bc = inB[29];
  //   _15bc = inB[30]; _16bc = inB[31]
endmodule
