// Digital circuit 16BitBSDShifter.dig as structural Verilog
module _16BitBSDShifter (
  input  [31:0] in,
  output [31:0] out,
  output [1:0] carry
);


  assign carry = in[31:30];
  assign out = {in[29:0], 2'b01};
endmodule
