// Digital circuit 16BitConverter.dig as structural Verilog
module _16BitConverter (
  input  [31:0] in,
  output [15:0] out,
  output carry
);

  wire or_1_out, or_2_out, or_3_out, or_4_out, or_5_out, or_6_out, or_7_out, or_8_out, or_9_out, or_10_out,
       or_11_out, or_12_out, or_13_out, or_14_out, or_15_out, or_16_out;
  wire [7:0] and_1_out, and_9_out, not_1_out, not_2_out;

  and and_1 (and_1_out[0], in[16], in[17]);
  or or_1 (or_1_out, in[16], in[17]);
  and and_2 (and_1_out[1], in[18], in[19]);
  or or_2 (or_2_out, in[18], in[19]);
  and and_3 (and_1_out[2], in[20], in[21]);
  or or_3 (or_3_out, in[20], in[21]);
  and and_4 (and_1_out[3], in[22], in[23]);
  or or_4 (or_4_out, in[22], in[23]);
  and and_5 (and_1_out[4], in[24], in[25]);
  or or_5 (or_5_out, in[24], in[25]);
  and and_6 (and_1_out[5], in[26], in[27]);
  or or_6 (or_6_out, in[26], in[27]);
  and and_7 (and_1_out[6], in[28], in[29]);
  or or_7 (or_7_out, in[28], in[29]);
  and and_8 (and_1_out[7], in[30], in[31]);
  or or_8 (or_8_out, in[30], in[31]);
  and and_9 (and_9_out[0], in[0], in[1]);
  or or_9 (or_9_out, in[0], in[1]);
  not not_1 (not_1_out[0], or_9_out);
  and and_10 (and_9_out[1], in[2], in[3]);
  or or_10 (or_10_out, in[2], in[3]);
  and and_11 (and_9_out[2], in[4], in[5]);
  or or_11 (or_11_out, in[4], in[5]);
  and and_12 (and_9_out[3], in[6], in[7]);
  or or_12 (or_12_out, in[6], in[7]);
  and and_13 (and_9_out[4], in[8], in[9]);
  or or_13 (or_13_out, in[8], in[9]);
  and and_14 (and_9_out[5], in[10], in[11]);
  or or_14 (or_14_out, in[10], in[11]);
  and and_15 (and_9_out[6], in[12], in[13]);
  or or_15 (or_15_out, in[12], in[13]);
  and and_16 (and_9_out[7], in[14], in[15]);
  or or_16 (or_16_out, in[14], in[15]);
  not not_2 (not_2_out[0], or_1_out);
  not not_3 (not_2_out[1], or_2_out);
  not not_4 (not_2_out[2], or_3_out);
  not not_5 (not_2_out[3], or_4_out);
  not not_6 (not_2_out[4], or_5_out);
  not not_7 (not_2_out[5], or_6_out);
  not not_8 (not_2_out[6], or_7_out);
  not not_9 (not_2_out[7], or_8_out);
  not not_10 (not_1_out[1], or_10_out);
  not not_11 (not_1_out[2], or_11_out);
  not not_12 (not_1_out[3], or_12_out);
  not not_13 (not_1_out[4], or_13_out);
  not not_14 (not_1_out[5], or_14_out);
  not not_15 (not_1_out[6], or_15_out);
  not not_16 (not_1_out[7], or_16_out);
  Sub #(.Bits(16)) sub_1 (.a({and_1_out, and_9_out}), .b({not_2_out, not_1_out}), .c_i(1'b0), .s(out), .c_o(carry));
endmodule
