// Digital circuit 8bitTC16BitBSDAdder.dig as structural Verilog
module _8bitTC16BitBSDAdder (
  input  [7:0] inTC,
  input  [31:0] inBSD,
  output [31:0] bsdOut,
  output [1:0] c
);

  Add add_1 (.a(inBSD[30]), .b(inBSD[31]), .c_i(inTC[7]), .s(bsdOut[31]), .c_o(c[0]));
  Add add_2 (.a(inBSD[28]), .b(inBSD[29]), .c_i(inTC[7]), .s(bsdOut[29]), .c_o(bsdOut[30]));
  Add add_3 (.a(inBSD[26]), .b(inBSD[27]), .c_i(inTC[7]), .s(bsdOut[27]), .c_o(bsdOut[28]));
  Add add_4 (.a(inBSD[24]), .b(inBSD[25]), .c_i(inTC[7]), .s(bsdOut[25]), .c_o(bsdOut[26]));
  not not_1 (c[1], inTC[7]);
  Add add_5 (.a(inBSD[22]), .b(inBSD[23]), .c_i(inTC[7]), .s(bsdOut[23]), .c_o(bsdOut[24]));
  Add add_6 (.a(inBSD[20]), .b(inBSD[21]), .c_i(inTC[7]), .s(bsdOut[21]), .c_o(bsdOut[22]));
  Add add_7 (.a(inBSD[18]), .b(inBSD[19]), .c_i(inTC[7]), .s(bsdOut[19]), .c_o(bsdOut[20]));
  Add add_8 (.a(inBSD[16]), .b(inBSD[17]), .c_i(inTC[7]), .s(bsdOut[17]), .c_o(bsdOut[18]));
  Add add_9 (.a(inBSD[14]), .b(inBSD[15]), .c_i(inTC[7]), .s(bsdOut[15]), .c_o(bsdOut[16]));
  Add add_10 (.a(inBSD[12]), .b(inBSD[13]), .c_i(inTC[6]), .s(bsdOut[13]), .c_o(bsdOut[14]));
  Add add_11 (.a(inBSD[10]), .b(inBSD[11]), .c_i(inTC[5]), .s(bsdOut[11]), .c_o(bsdOut[12]));
  Add add_12 (.a(inBSD[8]), .b(inBSD[9]), .c_i(inTC[4]), .s(bsdOut[9]), .c_o(bsdOut[10]));
  Add add_13 (.a(inBSD[6]), .b(inBSD[7]), .c_i(inTC[3]), .s(bsdOut[7]), .c_o(bsdOut[8]));
  Add add_14 (.a(inBSD[4]), .b(inBSD[5]), .c_i(inTC[2]), .s(bsdOut[5]), .c_o(bsdOut[6]));
  Add add_15 (.a(inBSD[2]), .b(inBSD[3]), .c_i(inTC[1]), .s(bsdOut[3]), .c_o(bsdOut[4]));
  Add add_16 (.a(inBSD[0]), .b(inBSD[1]), .c_i(inTC[0]), .s(bsdOut[1]), .c_o(bsdOut[2]));

  assign bsdOut[0] = 1'b0;
endmodule
