// Digital circuit 8bitTCtoBDC.dig as structural Verilog
module _8bitTCtoBDC (
  input  [7:0] in,
  output [15:0] _16bdd
);

  not not_1 (_16bdd[15], in[7]);

  assign _16bdd[14:0] = {2'b01, in[6], 1'b1, in[5], 1'b1, in[4], 1'b1, in[3], 1'b1, in[2], 1'b1, in[1], 1'b1, in[0]};
endmodule
