// Digital circuit conv3x316BitBSDAdder.dig as structural Verilog
module conv3x316BitBSDAdder (
  input  [7:0] w3,
  input  [7:0] w4,
  input  [7:0] w5,
  input  [7:0] w6,
  input  [7:0] w7,
  input  [7:0] w8,
  input  [7:0] w9,
  input  inClock,
  input  [7:0] w1,
  input  [7:0] w2,
  input  en,
  input  [7:0] w21,
  input  [7:0] w22,
  input  [7:0] w23,
  input  [7:0] w24,
  input  [7:0] w25,
  input  [7:0] w26,
  input  [7:0] w27,
  input  inClock_2,
  input  [7:0] w19,
  input  [7:0] w20,
  input  en_2,
  input  [7:0] w30,
  input  [7:0] w31,
  input  [7:0] w32,
  input  [7:0] w33,
  input  [7:0] w34,
  input  [7:0] w35,
  input  [7:0] w36,
  input  inClock_3,
  input  [7:0] w28,
  input  [7:0] w29,
  input  en_3,
  output [15:0] result,
  output cout,
  output [15:0] result_2,
  output cout_2,
  output [15:0] result_3,
  output cout_3
);

  wire clock2, clock4, not_1_out, not_2_out, not_3_out, register_1_q, register_2_q, register_3_q;
  wire [2:0] counter_1_out, counter_2_out, counter_3_out;
  wire [7:0] Kernel_2_d, Kernel_3_d, Kernel_d;
  wire [8:0] multiplexer_7_out, multiplexer_8_out, multiplexer_9_out;
  wire [15:0] _8bittctobdc_1__16bdd;
  wire [31:0] _8bittc16bitbsdadder_1_bsdout, _8bittc16bitbsdadder_2_bsdout, _16bitbsd_1_out,
       _16bitbsdextender_1_out, _16bitbsdshifter_1_out, _16bitbsdshifter_2_out, _16bitbsdshifter_3_out,
       multiplexer_28_out, multiplexer_29_out, multiplexer_30_out, register_4_q, register_5_q, register_6_q;

  and and_1 (clock2, inClock, en);
  and and_2 (clock4, inClock_2, en_2);
  and and_3 (clock4, inClock_3, en_3);
  Counter #(.Bits(3)) counter_1 (.en(1'b1), .C(clock2), .clr(not_1_out), .out(counter_1_out));  // open: ovf
  Multiplexer #(.Selector_Bits(3)) multiplexer_1 (
    .sel(counter_1_out), .in_0(w1[7]), .in_1(w1[6]), .in_2(w1[5]), .in_3(w1[4]), .in_4(w1[3]), .in_5(w1[2]),
    .in_6(w1[1]), .in_7(w1[0]), .out(multiplexer_7_out[8]));
  Counter #(.Bits(3)) counter_2 (.en(1'b1), .C(clock4), .clr(not_2_out), .out(counter_2_out));  // open: ovf
  Counter #(.Bits(3)) counter_3 (.en(1'b1), .C(clock4), .clr(not_3_out), .out(counter_3_out));  // open: ovf
  Multiplexer #(.Selector_Bits(3)) multiplexer_2 (
    .sel(counter_2_out), .in_0(w19[7]), .in_1(w19[6]), .in_2(w19[5]), .in_3(w19[4]), .in_4(w19[3]),
    .in_5(w19[2]), .in_6(w19[1]), .in_7(w19[0]), .out(multiplexer_8_out[8]));
  Multiplexer #(.Selector_Bits(3)) multiplexer_3 (
    .sel(counter_3_out), .in_0(w28[7]), .in_1(w28[6]), .in_2(w28[5]), .in_3(w28[4]), .in_4(w28[3]),
    .in_5(w28[2]), .in_6(w28[1]), .in_7(w28[0]), .out(multiplexer_9_out[8]));
  Multiplexer #(.Selector_Bits(3)) multiplexer_4 (
    .sel(counter_1_out), .in_0(w2[7]), .in_1(w2[6]), .in_2(w2[5]), .in_3(w2[4]), .in_4(w2[3]), .in_5(w2[2]),
    .in_6(w2[1]), .in_7(w2[0]), .out(multiplexer_7_out[7]));
  Multiplexer #(.Selector_Bits(3)) multiplexer_5 (
    .sel(counter_2_out), .in_0(w20[7]), .in_1(w20[6]), .in_2(w20[5]), .in_3(w20[4]), .in_4(w20[3]),
    .in_5(w20[2]), .in_6(w20[1]), .in_7(w20[0]), .out(multiplexer_8_out[7]));
  Multiplexer #(.Selector_Bits(3)) multiplexer_6 (
    .sel(counter_3_out), .in_0(w29[7]), .in_1(w29[6]), .in_2(w29[5]), .in_3(w29[4]), .in_4(w29[3]),
    .in_5(w29[2]), .in_6(w29[1]), .in_7(w29[0]), .out(multiplexer_9_out[7]));
  Multiplexer #(.Selector_Bits(3)) multiplexer_7 (
    .sel(counter_1_out), .in_0(w3[7]), .in_1(w3[6]), .in_2(w3[5]), .in_3(w3[4]), .in_4(w3[3]), .in_5(w3[2]),
    .in_6(w3[1]), .in_7(w3[0]), .out(multiplexer_7_out[6]));
  Multiplexer #(.Selector_Bits(3)) multiplexer_8 (
    .sel(counter_2_out), .in_0(w21[7]), .in_1(w21[6]), .in_2(w21[5]), .in_3(w21[4]), .in_4(w21[3]),
    .in_5(w21[2]), .in_6(w21[1]), .in_7(w21[0]), .out(multiplexer_8_out[6]));
  Multiplexer #(.Selector_Bits(3)) multiplexer_9 (
    .sel(counter_3_out), .in_0(w30[7]), .in_1(w30[6]), .in_2(w30[5]), .in_3(w30[4]), .in_4(w30[3]),
    .in_5(w30[2]), .in_6(w30[1]), .in_7(w30[0]), .out(multiplexer_9_out[6]));
  Multiplexer #(.Selector_Bits(3)) multiplexer_10 (
    .sel(counter_1_out), .in_0(w4[7]), .in_1(w4[6]), .in_2(w4[5]), .in_3(w4[4]), .in_4(w4[3]), .in_5(w4[2]),
    .in_6(w4[1]), .in_7(w4[0]), .out(multiplexer_7_out[5]));
  Multiplexer #(.Selector_Bits(3)) multiplexer_11 (
    .sel(counter_2_out), .in_0(w22[7]), .in_1(w22[6]), .in_2(w22[5]), .in_3(w22[4]), .in_4(w22[3]),
    .in_5(w22[2]), .in_6(w22[1]), .in_7(w22[0]), .out(multiplexer_8_out[5]));
  Multiplexer #(.Selector_Bits(3)) multiplexer_12 (
    .sel(counter_3_out), .in_0(w31[7]), .in_1(w31[6]), .in_2(w31[5]), .in_3(w31[4]), .in_4(w31[3]),
    .in_5(w31[2]), .in_6(w31[1]), .in_7(w31[0]), .out(multiplexer_9_out[5]));
  Multiplexer #(.Selector_Bits(3)) multiplexer_13 (
    .sel(counter_1_out), .in_0(w5[7]), .in_1(w5[6]), .in_2(w5[5]), .in_3(w5[4]), .in_4(w5[3]), .in_5(w5[2]),
    .in_6(w5[1]), .in_7(w5[0]), .out(multiplexer_7_out[4]));
  Multiplexer #(.Selector_Bits(3)) multiplexer_14 (
    .sel(counter_2_out), .in_0(w23[7]), .in_1(w23[6]), .in_2(w23[5]), .in_3(w23[4]), .in_4(w23[3]),
    .in_5(w23[2]), .in_6(w23[1]), .in_7(w23[0]), .out(multiplexer_8_out[4]));
  Multiplexer #(.Selector_Bits(3)) multiplexer_15 (
    .sel(counter_3_out), .in_0(w32[7]), .in_1(w32[6]), .in_2(w32[5]), .in_3(w32[4]), .in_4(w32[3]),
    .in_5(w32[2]), .in_6(w32[1]), .in_7(w32[0]), .out(multiplexer_9_out[4]));
  Multiplexer #(.Selector_Bits(3)) multiplexer_16 (
    .sel(counter_1_out), .in_0(w6[7]), .in_1(w6[6]), .in_2(w6[5]), .in_3(w6[4]), .in_4(w6[3]), .in_5(w6[2]),
    .in_6(w6[1]), .in_7(w6[0]), .out(multiplexer_7_out[3]));
  Multiplexer #(.Selector_Bits(3)) multiplexer_17 (
    .sel(counter_2_out), .in_0(w24[7]), .in_1(w24[6]), .in_2(w24[5]), .in_3(w24[4]), .in_4(w24[3]),
    .in_5(w24[2]), .in_6(w24[1]), .in_7(w24[0]), .out(multiplexer_8_out[3]));
  Multiplexer #(.Selector_Bits(3)) multiplexer_18 (
    .sel(counter_3_out), .in_0(w33[7]), .in_1(w33[6]), .in_2(w33[5]), .in_3(w33[4]), .in_4(w33[3]),
    .in_5(w33[2]), .in_6(w33[1]), .in_7(w33[0]), .out(multiplexer_9_out[3]));
  Multiplexer #(.Selector_Bits(3)) multiplexer_19 (
    .sel(counter_1_out), .in_0(w7[7]), .in_1(w7[6]), .in_2(w7[5]), .in_3(w7[4]), .in_4(w7[3]), .in_5(w7[2]),
    .in_6(w7[1]), .in_7(w7[0]), .out(multiplexer_7_out[2]));
  Multiplexer #(.Selector_Bits(3)) multiplexer_20 (
    .sel(counter_2_out), .in_0(w25[7]), .in_1(w25[6]), .in_2(w25[5]), .in_3(w25[4]), .in_4(w25[3]),
    .in_5(w25[2]), .in_6(w25[1]), .in_7(w25[0]), .out(multiplexer_8_out[2]));
  Multiplexer #(.Selector_Bits(3)) multiplexer_21 (
    .sel(counter_3_out), .in_0(w34[7]), .in_1(w34[6]), .in_2(w34[5]), .in_3(w34[4]), .in_4(w34[3]),
    .in_5(w34[2]), .in_6(w34[1]), .in_7(w34[0]), .out(multiplexer_9_out[2]));
  Multiplexer #(.Selector_Bits(3)) multiplexer_22 (
    .sel(counter_1_out), .in_0(w8[7]), .in_1(w8[6]), .in_2(w8[5]), .in_3(w8[4]), .in_4(w8[3]), .in_5(w8[2]),
    .in_6(w8[1]), .in_7(w8[0]), .out(multiplexer_7_out[1]));
  Multiplexer #(.Selector_Bits(3)) multiplexer_23 (
    .sel(counter_2_out), .in_0(w26[7]), .in_1(w26[6]), .in_2(w26[5]), .in_3(w26[4]), .in_4(w26[3]),
    .in_5(w26[2]), .in_6(w26[1]), .in_7(w26[0]), .out(multiplexer_8_out[1]));
  Multiplexer #(.Selector_Bits(3)) multiplexer_24 (
    .sel(counter_3_out), .in_0(w35[7]), .in_1(w35[6]), .in_2(w35[5]), .in_3(w35[4]), .in_4(w35[3]),
    .in_5(w35[2]), .in_6(w35[1]), .in_7(w35[0]), .out(multiplexer_9_out[1]));
  Multiplexer #(.Selector_Bits(3)) multiplexer_25 (
    .sel(counter_1_out), .in_0(w9[7]), .in_1(w9[6]), .in_2(w9[5]), .in_3(w9[4]), .in_4(w9[3]), .in_5(w9[2]),
    .in_6(w9[1]), .in_7(w9[0]), .out(multiplexer_7_out[0]));
  Register register_1 (.D(1'b1), .C(clock2), .en(1'b1), .Q(register_1_q));
  Multiplexer #(.Selector_Bits(3)) multiplexer_26 (
    .sel(counter_2_out), .in_0(w27[7]), .in_1(w27[6]), .in_2(w27[5]), .in_3(w27[4]), .in_4(w27[3]),
    .in_5(w27[2]), .in_6(w27[1]), .in_7(w27[0]), .out(multiplexer_8_out[0]));
  Multiplexer #(.Selector_Bits(3)) multiplexer_27 (
    .sel(counter_3_out), .in_0(w36[7]), .in_1(w36[6]), .in_2(w36[5]), .in_3(w36[4]), .in_4(w36[3]),
    .in_5(w36[2]), .in_6(w36[1]), .in_7(w36[0]), .out(multiplexer_9_out[0]));
  ROM #(.AddrBits(9), .isProgramMemory("true"), .Bits(8)) Kernel (.A(multiplexer_7_out), .sel(1'b1), .D(Kernel_d));
  not not_1 (not_1_out, register_1_q);
  Register register_2 (.D(1'b1), .C(clock4), .en(1'b1), .Q(register_2_q));
  Register register_3 (.D(1'b1), .C(clock4), .en(1'b1), .Q(register_3_q));
  _8bitTCtoBDC _8bittctobdc_1 (.in(Kernel_d), ._16bdd(_8bittctobdc_1__16bdd));
  _16BitBSDExtender _16bitbsdextender_1 (.in(_8bittctobdc_1__16bdd), .out(_16bitbsdextender_1_out));
  Multiplexer #(.Bits(32)) multiplexer_28 (
    .sel(not_1_out), .in_0(_16bitbsd_1_out), .in_1(32'h55555555), .out(multiplexer_28_out));
  ROM #(.AddrBits(9), .isProgramMemory("true"), .Bits(8)) Kernel_2 (.A(multiplexer_8_out), .sel(1'b1), .D(Kernel_2_d));
  not not_2 (not_2_out, register_2_q);
  ROM #(.AddrBits(9), .isProgramMemory("true"), .Bits(8)) Kernel_3 (.A(multiplexer_9_out), .sel(1'b1), .D(Kernel_3_d));
  not not_3 (not_3_out, register_3_q);
  Multiplexer #(.Bits(32)) multiplexer_29 (
    .sel(not_2_out), .in_0(_8bittc16bitbsdadder_1_bsdout), .in_1(32'h55555555), .out(multiplexer_29_out));
  Multiplexer #(.Bits(32)) multiplexer_30 (
    .sel(not_3_out), .in_0(_8bittc16bitbsdadder_2_bsdout), .in_1(32'h55555555), .out(multiplexer_30_out));
  _16BitBSD _16bitbsd_1 (
    .inA(_16bitbsdshifter_1_out), .inB(_16bitbsdextender_1_out), .out(_16bitbsd_1_out));  // open: carry
  _8bitTC16BitBSDAdder _8bittc16bitbsdadder_1 (
    .inTC(Kernel_2_d), .inBSD(_16bitbsdshifter_2_out), .bsdOut(_8bittc16bitbsdadder_1_bsdout));  // open: c
  _8bitTC16BitBSDAdder _8bittc16bitbsdadder_2 (
    .inTC(Kernel_3_d), .inBSD(_16bitbsdshifter_3_out), .bsdOut(_8bittc16bitbsdadder_2_bsdout));  // open: c
  Register #(.Bits(32)) register_4 (.D(multiplexer_28_out), .C(clock2), .en(1'b1), .Q(register_4_q));
  Register #(.Bits(32)) register_5 (.D(multiplexer_29_out), .C(clock4), .en(1'b1), .Q(register_5_q));
  Register #(.Bits(32)) register_6 (.D(multiplexer_30_out), .C(clock4), .en(1'b1), .Q(register_6_q));
  _16BitBSDShifter _16bitbsdshifter_1 (.in(register_4_q), .out(_16bitbsdshifter_1_out));  // open: carry
  _16BitConverter _16bitconverter_1 (.in(register_4_q), .out(result), .carry(cout));
  _16BitBSDShifter _16bitbsdshifter_2 (.in(register_5_q), .out(_16bitbsdshifter_2_out));  // open: carry
  _16BitBSDShifter _16bitbsdshifter_3 (.in(register_6_q), .out(_16bitbsdshifter_3_out));  // open: carry
  _16BitConverter _16bitconverter_2 (.in(register_5_q), .out(result_2), .carry(cout_2));
  _16BitConverter _16bitconverter_3 (.in(register_6_q), .out(result_3), .carry(cout_3));

  // Notes on the sheet:
  //   inClock: clock input
  //   inClock_2: clock input
  //   inClock_3: clock input
  //   Allgemeiner fall mit 16 bit adder (für grosse filter) 3x3 convoltion
  //   w3
  //   w5
  //   w4
  //   w6
  //   w7
  //   w8
  //   w9
  //   8 TC digit Rom wort breite
  //   //wird jetzt in TC abgelegt
  //   contents of Kernel (hex, n*v repeats v):
  //   0,1,2,3,1,2,3,4,2,3,4,5,3,4,5,6,4,5,6,7,5,6,7,8,6,7,8,9,7,8,9
  //   ,a,2,3,4,5,3,4,5,6,4,5,6,7,5,6,7,8,6,7,8,9,7,8,9,a,8,9,a,b,9,a
  //   ,b,c,1,2,3,4,2,3,4,5,3,4,5,6,4,5,6,7,5,6,7,8,6,7,8,9,7,8,9,a,8
  //   ,9,a,b,3,4,5,6,4,5,6,7,5,6,7,8,6,7,8,9,7,8,9,a,8,9,a,b,9,a,b,c
  //   ,a,b,c,d,2,3,4,5,3,4,5,6,4,5,6,7,5,6,7,8,6,7,8,9,7,8,9,a,8,9,a
  //   ,b,9,a,b,c,4,5,6,7,5,6,7,8,6,7,8,9,7,8,9,a,8,9,a,b,9,a,b,c,a,b
  //   ,c,d,b,c,d,e,3,4,5,6,4,5,6,7,5,6,7,8,6,7,8,9,7,8,9,a,8,9,a,b,9
  //   ,a,b,c,a,b,c,d,5,6,7,8,6,7,8,9,7,8,9,a,8,9,a,b,9,a,b,c,a,b,c,d
  //   ,b,c,d,e,c,d,e,f,1,2,3,4,2,3,4,5,3,4,5,6,4,5,6,7,5,6,7,8,6,7,8
  //   ,9,7,8,9,a,8,9,a,b,3,4,5,6,4,5,6,7,5,6,7,8,6,7,8,9,7,8,9,a,8,9
  //   ,a,b,9,a,b,c,a,b,c,d,2,3,4,5,3,4,5,6,4,5,6,7,5,6,7,8,6,7,8,9,7
  //   ,8,9,a,8,9,a,b,9,a,b,c,4,5,6,7,5,6,7,8,6,7,8,9,7,8,9,a,8,9,a,b
  //   ,9,a,b,c,a,b,c,d,b,c,d,e,3,4,5,6,4,5,6,7,5,6,7,8,6,7,8,9,7,8,9
  //   ,a,8,9,a,b,9,a,b,c,a,b,c,d,5,6,7,8,6,7,8,9,7,8,9,a,8,9,a,b,9,a
  //   ,b,c,a,b,c,d,b,c,d,e,c,d,e,f,4,5,6,7,5,6,7,8,6,7,8,9,7,8,9,a,8
  //   ,9,a,b,9,a,b,c,a,b,c,d,b,c,d,e,6,7,8,9,7,8,9,a,8,9,a,b,9,a,b,c
  //   ,a,b,c,d,b,c,d,e,c,d,e,f,d,e,f,10
  //   contents of Kernel_2 (hex, n*v repeats v):
  //   0,1,2,3,1,2,3,4,2,3,4,5,3,4,5,6,4,5,6,7,5,6,7,8,6,7,8,9,7,8,9
  //   ,a,2,3,4,5,3,4,5,6,4,5,6,7,5,6,7,8,6,7,8,9,7,8,9,a,8,9,a,b,9,a
  //   ,b,c,1,2,3,4,2,3,4,5,3,4,5,6,4,5,6,7,5,6,7,8,6,7,8,9,7,8,9,a,8
  //   ,9,a,b,3,4,5,6,4,5,6,7,5,6,7,8,6,7,8,9,7,8,9,a,8,9,a,b,9,a,b,c
  //   ,a,b,c,d,2,3,4,5,3,4,5,6,4,5,6,7,5,6,7,8,6,7,8,9,7,8,9,a,8,9,a
  //   ,b,9,a,b,c,4,5,6,7,5,6,7,8,6,7,8,9,7,8,9,a,8,9,a,b,9,a,b,c,a,b
  //   ,c,d,b,c,d,e,3,4,5,6,4,5,6,7,5,6,7,8,6,7,8,9,7,8,9,a,8,9,a,b,9
  //   ,a,b,c,a,b,c,d,5,6,7,8,6,7,8,9,7,8,9,a,8,9,a,b,9,a,b,c,a,b,c,d
  //   ,b,c,d,e,c,d,e,f,1,2,3,4,2,3,4,5,3,4,5,6,4,5,6,7,5,6,7,8,6,7,8
  //   ,9,7,8,9,a,8,9,a,b,3,4,5,6,4,5,6,7,5,6,7,8,6,7,8,9,7,8,9,a,8,9
  //   ,a,b,9,a,b,c,a,b,c,d,2,3,4,5,3,4,5,6,4,5,6,7,5,6,7,8,6,7,8,9,7
  //   ,8,9,a,8,9,a,b,9,a,b,c,4,5,6,7,5,6,7,8,6,7,8,9,7,8,9,a,8,9,a,b
  //   ,9,a,b,c,a,b,c,d,b,c,d,e,3,4,5,6,4,5,6,7,5,6,7,8,6,7,8,9,7,8,9
  //   ,a,8,9,a,b,9,a,b,c,a,b,c,d,5,6,7,8,6,7,8,9,7,8,9,a,8,9,a,b,9,a
  //   ,b,c,a,b,c,d,b,c,d,e,c,d,e,f,4,5,6,7,5,6,7,8,6,7,8,9,7,8,9,a,8
  //   ,9,a,b,9,a,b,c,a,b,c,d,b,c,d,e,6,7,8,9,7,8,9,a,8,9,a,b,9,a,b,c
  //   ,a,b,c,d,b,c,d,e,c,d,e,f,d,e,f,10
  //   contents of Kernel_3 (hex, n*v repeats v):
  //   0,1,2,3,1,2,3,4,2,3,4,5,3,4,5,6,4,5,6,7,5,6,7,8,6,7,8,9,7,8,9
  //   ,a,2,3,4,5,3,4,5,6,4,5,6,7,5,6,7,8,6,7,8,9,7,8,9,a,8,9,a,b,9,a
  //   ,b,c,1,2,3,4,2,3,4,5,3,4,5,6,4,5,6,7,5,6,7,8,6,7,8,9,7,8,9,a,8
  //   ,9,a,b,3,4,5,6,4,5,6,7,5,6,7,8,6,7,8,9,7,8,9,a,8,9,a,b,9,a,b,c
  //   ,a,b,c,d,2,3,4,5,3,4,5,6,4,5,6,7,5,6,7,8,6,7,8,9,7,8,9,a,8,9,a
  //   ,b,9,a,b,c,4,5,6,7,5,6,7,8,6,7,8,9,7,8,9,a,8,9,a,b,9,a,b,c,a,b
  //   ,c,d,b,c,d,e,3,4,5,6,4,5,6,7,5,6,7,8,6,7,8,9,7,8,9,a,8,9,a,b,9
  //   ,a,b,c,a,b,c,d,5,6,7,8,6,7,8,9,7,8,9,a,8,9,a,b,9,a,b,c,a,b,c,d
  //   ,b,c,d,e,c,d,e,f,1,2,3,4,2,3,4,5,3,4,5,6,4,5,6,7,5,6,7,8,6,7,8
  //   ,9,7,8,9,a,8,9,a,b,3,4,5,6,4,5,6,7,5,6,7,8,6,7,8,9,7,8,9,a,8,9
  //   ,a,b,9,a,b,c,a,b,c,d,2,3,4,5,3,4,5,6,4,5,6,7,5,6,7,8,6,7,8,9,7
  //   ,8,9,a,8,9,a,b,9,a,b,c,4,5,6,7,5,6,7,8,6,7,8,9,7,8,9,a,8,9,a,b
  //   ,9,a,b,c,a,b,c,d,b,c,d,e,3,4,5,6,4,5,6,7,5,6,7,8,6,7,8,9,7,8,9
  //   ,a,8,9,a,b,9,a,b,c,a,b,c,d,5,6,7,8,6,7,8,9,7,8,9,a,8,9,a,b,9,a
  //   ,b,c,a,b,c,d,b,c,d,e,c,d,e,f,4,5,6,7,5,6,7,8,6,7,8,9,7,8,9,a,8
  //   ,9,a,b,9,a,b,c,a,b,c,d,b,c,d,e,6,7,8,9,7,8,9,a,8,9,a,b,9,a,b,c
  //   ,a,b,c,d,b,c,d,e,c,d,e,f,d,e,f,10
endmodule
