// Digital circuit convoltiononalCircuit.dig as structural Verilog
module convoltiononalCircuit (
  input  in_1,
  input  in_2,
  input  [7:0] in_3,
  input  [7:0] in_4,
  input  [7:0] in_5,
  input  [7:0] in_6,
  output [7:0] out_7,
  output out_8,
  output [8:0] out_9
);

  wire [2:0] counter_1_out;
  wire [3:0] multiplexer_1_out;
  wire [8:0] add_1_s, barrelshifter_1_out, bitextender_1_out;

  Counter #(.Bits(3)) counter_1 (.en(1'b1), .C(in_1), .clr(in_2), .out(counter_1_out));  // open: ovf
  Multiplexer #(.Selector_Bits(3)) multiplexer_1 (
    .sel(counter_1_out), .in_0(in_3[7]), .in_1(in_3[6]), .in_2(in_3[5]), .in_3(in_3[4]), .in_4(in_3[3]),
    .in_5(in_3[2]), .in_6(in_3[1]), .in_7(in_3[0]), .out(multiplexer_1_out[3]));
  Multiplexer #(.Selector_Bits(3)) multiplexer_2 (
    .sel(counter_1_out), .in_0(in_4[7]), .in_1(in_4[6]), .in_2(in_4[5]), .in_3(in_4[4]), .in_4(in_4[3]),
    .in_5(in_4[2]), .in_6(in_4[1]), .in_7(in_4[0]), .out(multiplexer_1_out[1]));
  Multiplexer #(.Selector_Bits(3)) multiplexer_3 (
    .sel(counter_1_out), .in_0(in_6[7]), .in_1(in_6[6]), .in_2(in_6[5]), .in_3(in_6[4]), .in_4(in_6[3]),
    .in_5(in_6[2]), .in_6(in_6[1]), .in_7(in_6[0]), .out(multiplexer_1_out[2]));
  Multiplexer #(.Selector_Bits(3)) multiplexer_4 (
    .sel(counter_1_out), .in_0(in_5[7]), .in_1(in_5[6]), .in_2(in_5[5]), .in_3(in_5[4]), .in_4(in_5[3]),
    .in_5(in_5[2]), .in_6(in_5[1]), .in_7(in_5[0]), .out(multiplexer_1_out[0]));
  Register #(.Bits(9)) register_1 (.D(add_1_s), .C(in_1), .en(1'b1), .Q(out_9));
  ROM #(.AddrBits(4), .Bits(8)) rom_1 (.A(multiplexer_1_out), .sel(1'b1), .D(out_7));
  BitExtender #(.outputBits(9)) bitextender_1 (.in(out_7), .out(bitextender_1_out));
  BarrelShifter #(.Bits(9)) barrelshifter_1 (.in(out_9), .shift(4'b0001), .out(barrelshifter_1_out));
  Add #(.Bits(9)) add_1 (.a(barrelshifter_1_out), .b(bitextender_1_out), .c_i(1'b0), .s(add_1_s), .c_o(out_8));

  // Notes on the sheet:
  //   notmale 2s complement schaltung
  //   mit 8 bit pixel values
  //   => 4 bildpunkten => 16 adressen Rom translation
  //   Pixel1
  //   Allgemeiner fall mit 16 bit adder (für grosse filter)
  //   Pixel2
  //   Pixel4
  //   Pre calculatet values in BSD format von w1 + w2 + .. an aber normal binary abgelegten adressen
  //   akk ist jetzt bsd Darstellung 010101...
  //   contents of rom_1 (hex, n*v repeats v):
  //   0,ffffffffffffffff,ffffffffffffffff,fffffffffffffffe,1,0,0,ffffffffffffffff
  //   ,1,0,0,ffffffffffffffff,2,1,1
  //   wird jetzt BSD shifter der 01 hinten anhängt
  //   bsd adder addiert jetzt ROM abgelegent bsd wert
  //   (im wohl codierten format) mit bsd akkumulator
endmodule
