// Digital circuit 5BitTCBSDConvcesion.dig as structural Verilog
module _5BitTCBSDConvcesion (
  input  [4:0] in,
  output [15:0] _10bdd
);

  // Pins of 10 and 16 bits meet at {_10bdd[15:10], 1'b1, in[4], 1'b1, in[3], 1'b1, in[2], 1'b1, in[1], 1'b1, in[0]}

  assign _10bdd[9:0] = {1'b1, in[4], 1'b1, in[3], 1'b1, in[2], 1'b1, in[1], 1'b1, in[0]};
endmodule
