// Digital circuit 6BitBCDTC.dig as structural Verilog
module _6BitBCDTC (
  input  [5:0] inTC,
  input  [11:0] inBSD,
  output [11:0] bsdOut,
  output [1:0] carryOut
);

  Add add_1 (.a(inBSD[10]), .b(inBSD[11]), .c_i(inTC[5]), .s(bsdOut[11]), .c_o(carryOut[0]));
  Add add_2 (.a(inBSD[8]), .b(inBSD[9]), .c_i(inTC[4]), .s(bsdOut[9]), .c_o(bsdOut[10]));
  not not_1 (carryOut[1], inTC[5]);
  Add add_3 (.a(inBSD[6]), .b(inBSD[7]), .c_i(inTC[3]), .s(bsdOut[7]), .c_o(bsdOut[8]));
  Add add_4 (.a(inBSD[4]), .b(inBSD[5]), .c_i(inTC[2]), .s(bsdOut[5]), .c_o(bsdOut[6]));
  Add add_5 (.a(inBSD[2]), .b(inBSD[3]), .c_i(inTC[1]), .s(bsdOut[3]), .c_o(bsdOut[4]));
  Add add_6 (.a(inBSD[0]), .b(inBSD[1]), .c_i(inTC[0]), .s(bsdOut[1]), .c_o(bsdOut[2]));

  assign bsdOut[0] = 1'b0;
endmodule
