// Digital circuit ParralelRomGaussian.dig as structural Verilog
module ParralelRomGaussian (
  input  [8:0] in0,
  input  [8:0] in1,
  input  [8:0] in2,
  input  [8:0] in3,
  input  [8:0] in4,
  input  [8:0] in5,
  input  [8:0] in6,
  input  [8:0] in7,
  output [4:0] out0,
  output [4:0] out1,
  output [4:0] out2,
  output [4:0] out3,
  output [4:0] out4,
  output [4:0] out5,
  output [4:0] out6,
  output [4:0] out7
);

  ROM #(.AddrBits(9), .isProgramMemory("true"), .Bits(5)) Kernel (.A(in0), .sel(1'b1), .D(out0));
  ROM #(.AddrBits(9), .isProgramMemory("true"), .Bits(5)) Kernel_2 (.A(in1), .sel(1'b1), .D(out1));
  ROM #(.AddrBits(9), .isProgramMemory("true"), .Bits(5)) Kernel_3 (.A(in2), .sel(1'b1), .D(out2));
  ROM #(.AddrBits(9), .isProgramMemory("true"), .Bits(5)) Kernel_4 (.A(in3), .sel(1'b1), .D(out3));
  ROM #(.AddrBits(9), .isProgramMemory("true"), .Bits(5)) Kernel_5 (.A(in4), .sel(1'b1), .D(out4));
  ROM #(.AddrBits(9), .isProgramMemory("true"), .Bits(5)) Kernel_6 (.A(in5), .sel(1'b1), .D(out5));
  ROM #(.AddrBits(9), .isProgramMemory("true"), .Bits(5)) Kernel_7 (.A(in6), .sel(1'b1), .D(out6));
  ROM #(.AddrBits(9), .isProgramMemory("true"), .Bits(5)) Kernel_8 (.A(in7), .sel(1'b1), .D(out7));

  // Notes on the sheet:
  //   contents of Kernel (hex, n*v repeats v):
  //   0,1,2,3,1,2,3,4,2,3,4,5,3,4,5,6,4,5,6,7,5,6,7,8,6,7,8,9,7,8,9
  //   ,a,2,3,4,5,3,4,5,6,4,5,6,7,5,6,7,8,6,7,8,9,7,8,9,a,8,9,a,b,9,a
  //   ,b,c,1,2,3,4,2,3,4,5,3,4,5,6,4,5,6,7,5,6,7,8,6,7,8,9,7,8,9,a,8
  //   ,9,a,b,3,4,5,6,4,5,6,7,5,6,7,8,6,7,8,9,7,8,9,a,8,9,a,b,9,a,b,c
  //   ,a,b,c,d,2,3,4,5,3,4,5,6,4,5,6,7,5,6,7,8,6,7,8,9,7,8,9,a,8,9,a
  //   ,b,9,a,b,c,4,5,6,7,5,6,7,8,6,7,8,9,7,8,9,a,8,9,a,b,9,a,b,c,a,b
  //   ,c,d,b,c,d,e,3,4,5,6,4,5,6,7,5,6,7,8,6,7,8,9,7,8,9,a,8,9,a,b,9
  //   ,a,b,c,a,b,c,d,5,6,7,8,6,7,8,9,7,8,9,a,8,9,a,b,9,a,b,c,a,b,c,d
  //   ,b,c,d,e,c,d,e,f,1,2,3,4,2,3,4,5,3,4,5,6,4,5,6,7,5,6,7,8,6,7,8
  //   ,9,7,8,9,a,8,9,a,b,3,4,5,6,4,5,6,7,5,6,7,8,6,7,8,9,7,8,9,a,8,9
  //   ,a,b,9,a,b,c,a,b,c,d,2,3,4,5,3,4,5,6,4,5,6,7,5,6,7,8,6,7,8,9,7
  //   ,8,9,a,8,9,a,b,9,a,b,c,4,5,6,7,5,6,7,8,6,7,8,9,7,8,9,a,8,9,a,b
  //   ,9,a,b,c,a,b,c,d,b,c,d,e,3,4,5,6,4,5,6,7,5,6,7,8,6,7,8,9,7,8,9
  //   ,a,8,9,a,b,9,a,b,c,a,b,c,d,5,6,7,8,6,7,8,9,7,8,9,a,8,9,a,b,9,a
  //   ,b,c,a,b,c,d,b,c,d,e,c,d,e,f,4,5,6,7,5,6,7,8,6,7,8,9,7,8,9,a,8
  //   ,9,a,b,9,a,b,c,a,b,c,d,b,c,d,e,6,7,8,9,7,8,9,a,8,9,a,b,9,a,b,c
  //   ,a,b,c,d,b,c,d,e,c,d,e,f,d,e,f,10
  //   contents of Kernel_2 (hex, n*v repeats v):
  //   0,1,2,3,1,2,3,4,2,3,4,5,3,4,5,6,4,5,6,7,5,6,7,8,6,7,8,9,7,8,9
  //   ,a,2,3,4,5,3,4,5,6,4,5,6,7,5,6,7,8,6,7,8,9,7,8,9,a,8,9,a,b,9,a
  //   ,b,c,1,2,3,4,2,3,4,5,3,4,5,6,4,5,6,7,5,6,7,8,6,7,8,9,7,8,9,a,8
  //   ,9,a,b,3,4,5,6,4,5,6,7,5,6,7,8,6,7,8,9,7,8,9,a,8,9,a,b,9,a,b,c
  //   ,a,b,c,d,2,3,4,5,3,4,5,6,4,5,6,7,5,6,7,8,6,7,8,9,7,8,9,a,8,9,a
  //   ,b,9,a,b,c,4,5,6,7,5,6,7,8,6,7,8,9,7,8,9,a,8,9,a,b,9,a,b,c,a,b
  //   ,c,d,b,c,d,e,3,4,5,6,4,5,6,7,5,6,7,8,6,7,8,9,7,8,9,a,8,9,a,b,9
  //   ,a,b,c,a,b,c,d,5,6,7,8,6,7,8,9,7,8,9,a,8,9,a,b,9,a,b,c,a,b,c,d
  //   ,b,c,d,e,c,d,e,f,1,2,3,4,2,3,4,5,3,4,5,6,4,5,6,7,5,6,7,8,6,7,8
  //   ,9,7,8,9,a,8,9,a,b,3,4,5,6,4,5,6,7,5,6,7,8,6,7,8,9,7,8,9,a,8,9
  //   ,a,b,9,a,b,c,a,b,c,d,2,3,4,5,3,4,5,6,4,5,6,7,5,6,7,8,6,7,8,9,7
  //   ,8,9,a,8,9,a,b,9,a,b,c,4,5,6,7,5,6,7,8,6,7,8,9,7,8,9,a,8,9,a,b
  //   ,9,a,b,c,a,b,c,d,b,c,d,e,3,4,5,6,4,5,6,7,5,6,7,8,6,7,8,9,7,8,9
  //   ,a,8,9,a,b,9,a,b,c,a,b,c,d,5,6,7,8,6,7,8,9,7,8,9,a,8,9,a,b,9,a
  //   ,b,c,a,b,c,d,b,c,d,e,c,d,e,f,4,5,6,7,5,6,7,8,6,7,8,9,7,8,9,a,8
  //   ,9,a,b,9,a,b,c,a,b,c,d,b,c,d,e,6,7,8,9,7,8,9,a,8,9,a,b,9,a,b,c
  //   ,a,b,c,d,b,c,d,e,c,d,e,f,d,e,f,10
  //   contents of Kernel_3 (hex, n*v repeats v):
  //   0,1,2,3,1,2,3,4,2,3,4,5,3,4,5,6,4,5,6,7,5,6,7,8,6,7,8,9,7,8,9
  //   ,a,2,3,4,5,3,4,5,6,4,5,6,7,5,6,7,8,6,7,8,9,7,8,9,a,8,9,a,b,9,a
  //   ,b,c,1,2,3,4,2,3,4,5,3,4,5,6,4,5,6,7,5,6,7,8,6,7,8,9,7,8,9,a,8
  //   ,9,a,b,3,4,5,6,4,5,6,7,5,6,7,8,6,7,8,9,7,8,9,a,8,9,a,b,9,a,b,c
  //   ,a,b,c,d,2,3,4,5,3,4,5,6,4,5,6,7,5,6,7,8,6,7,8,9,7,8,9,a,8,9,a
  //   ,b,9,a,b,c,4,5,6,7,5,6,7,8,6,7,8,9,7,8,9,a,8,9,a,b,9,a,b,c,a,b
  //   ,c,d,b,c,d,e,3,4,5,6,4,5,6,7,5,6,7,8,6,7,8,9,7,8,9,a,8,9,a,b,9
  //   ,a,b,c,a,b,c,d,5,6,7,8,6,7,8,9,7,8,9,a,8,9,a,b,9,a,b,c,a,b,c,d
  //   ,b,c,d,e,c,d,e,f,1,2,3,4,2,3,4,5,3,4,5,6,4,5,6,7,5,6,7,8,6,7,8
  //   ,9,7,8,9,a,8,9,a,b,3,4,5,6,4,5,6,7,5,6,7,8,6,7,8,9,7,8,9,a,8,9
  //   ,a,b,9,a,b,c,a,b,c,d,2,3,4,5,3,4,5,6,4,5,6,7,5,6,7,8,6,7,8,9,7
  //   ,8,9,a,8,9,a,b,9,a,b,c,4,5,6,7,5,6,7,8,6,7,8,9,7,8,9,a,8,9,a,b
  //   ,9,a,b,c,a,b,c,d,b,c,d,e,3,4,5,6,4,5,6,7,5,6,7,8,6,7,8,9,7,8,9
  //   ,a,8,9,a,b,9,a,b,c,a,b,c,d,5,6,7,8,6,7,8,9,7,8,9,a,8,9,a,b,9,a
  //   ,b,c,a,b,c,d,b,c,d,e,c,d,e,f,4,5,6,7,5,6,7,8,6,7,8,9,7,8,9,a,8
  //   ,9,a,b,9,a,b,c,a,b,c,d,b,c,d,e,6,7,8,9,7,8,9,a,8,9,a,b,9,a,b,c
  //   ,a,b,c,d,b,c,d,e,c,d,e,f,d,e,f,10
  //   contents of Kernel_4 (hex, n*v repeats v):
  //   0,1,2,3,1,2,3,4,2,3,4,5,3,4,5,6,4,5,6,7,5,6,7,8,6,7,8,9,7,8,9
  //   ,a,2,3,4,5,3,4,5,6,4,5,6,7,5,6,7,8,6,7,8,9,7,8,9,a,8,9,a,b,9,a
  //   ,b,c,1,2,3,4,2,3,4,5,3,4,5,6,4,5,6,7,5,6,7,8,6,7,8,9,7,8,9,a,8
  //   ,9,a,b,3,4,5,6,4,5,6,7,5,6,7,8,6,7,8,9,7,8,9,a,8,9,a,b,9,a,b,c
  //   ,a,b,c,d,2,3,4,5,3,4,5,6,4,5,6,7,5,6,7,8,6,7,8,9,7,8,9,a,8,9,a
  //   ,b,9,a,b,c,4,5,6,7,5,6,7,8,6,7,8,9,7,8,9,a,8,9,a,b,9,a,b,c,a,b
  //   ,c,d,b,c,d,e,3,4,5,6,4,5,6,7,5,6,7,8,6,7,8,9,7,8,9,a,8,9,a,b,9
  //   ,a,b,c,a,b,c,d,5,6,7,8,6,7,8,9,7,8,9,a,8,9,a,b,9,a,b,c,a,b,c,d
  //   ,b,c,d,e,c,d,e,f,1,2,3,4,2,3,4,5,3,4,5,6,4,5,6,7,5,6,7,8,6,7,8
  //   ,9,7,8,9,a,8,9,a,b,3,4,5,6,4,5,6,7,5,6,7,8,6,7,8,9,7,8,9,a,8,9
  //   ,a,b,9,a,b,c,a,b,c,d,2,3,4,5,3,4,5,6,4,5,6,7,5,6,7,8,6,7,8,9,7
  //   ,8,9,a,8,9,a,b,9,a,b,c,4,5,6,7,5,6,7,8,6,7,8,9,7,8,9,a,8,9,a,b
  //   ,9,a,b,c,a,b,c,d,b,c,d,e,3,4,5,6,4,5,6,7,5,6,7,8,6,7,8,9,7,8,9
  //   ,a,8,9,a,b,9,a,b,c,a,b,c,d,5,6,7,8,6,7,8,9,7,8,9,a,8,9,a,b,9,a
  //   ,b,c,a,b,c,d,b,c,d,e,c,d,e,f,4,5,6,7,5,6,7,8,6,7,8,9,7,8,9,a,8
  //   ,9,a,b,9,a,b,c,a,b,c,d,b,c,d,e,6,7,8,9,7,8,9,a,8,9,a,b,9,a,b,c
  //   ,a,b,c,d,b,c,d,e,c,d,e,f,d,e,f,10
  //   contents of Kernel_5 (hex, n*v repeats v):
  //   0,1,2,3,1,2,3,4,2,3,4,5,3,4,5,6,4,5,6,7,5,6,7,8,6,7,8,9,7,8,9
  //   ,a,2,3,4,5,3,4,5,6,4,5,6,7,5,6,7,8,6,7,8,9,7,8,9,a,8,9,a,b,9,a
  //   ,b,c,1,2,3,4,2,3,4,5,3,4,5,6,4,5,6,7,5,6,7,8,6,7,8,9,7,8,9,a,8
  //   ,9,a,b,3,4,5,6,4,5,6,7,5,6,7,8,6,7,8,9,7,8,9,a,8,9,a,b,9,a,b,c
  //   ,a,b,c,d,2,3,4,5,3,4,5,6,4,5,6,7,5,6,7,8,6,7,8,9,7,8,9,a,8,9,a
  //   ,b,9,a,b,c,4,5,6,7,5,6,7,8,6,7,8,9,7,8,9,a,8,9,a,b,9,a,b,c,a,b
  //   ,c,d,b,c,d,e,3,4,5,6,4,5,6,7,5,6,7,8,6,7,8,9,7,8,9,a,8,9,a,b,9
  //   ,a,b,c,a,b,c,d,5,6,7,8,6,7,8,9,7,8,9,a,8,9,a,b,9,a,b,c,a,b,c,d
  //   ,b,c,d,e,c,d,e,f,1,2,3,4,2,3,4,5,3,4,5,6,4,5,6,7,5,6,7,8,6,7,8
  //   ,9,7,8,9,a,8,9,a,b,3,4,5,6,4,5,6,7,5,6,7,8,6,7,8,9,7,8,9,a,8,9
  //   ,a,b,9,a,b,c,a,b,c,d,2,3,4,5,3,4,5,6,4,5,6,7,5,6,7,8,6,7,8,9,7
  //   ,8,9,a,8,9,a,b,9,a,b,c,4,5,6,7,5,6,7,8,6,7,8,9,7,8,9,a,8,9,a,b
  //   ,9,a,b,c,a,b,c,d,b,c,d,e,3,4,5,6,4,5,6,7,5,6,7,8,6,7,8,9,7,8,9
  //   ,a,8,9,a,b,9,a,b,c,a,b,c,d,5,6,7,8,6,7,8,9,7,8,9,a,8,9,a,b,9,a
  //   ,b,c,a,b,c,d,b,c,d,e,c,d,e,f,4,5,6,7,5,6,7,8,6,7,8,9,7,8,9,a,8
  //   ,9,a,b,9,a,b,c,a,b,c,d,b,c,d,e,6,7,8,9,7,8,9,a,8,9,a,b,9,a,b,c
  //   ,a,b,c,d,b,c,d,e,c,d,e,f,d,e,f,10
  //   contents of Kernel_6 (hex, n*v repeats v):
  //   0,1,2,3,1,2,3,4,2,3,4,5,3,4,5,6,4,5,6,7,5,6,7,8,6,7,8,9,7,8,9
  //   ,a,2,3,4,5,3,4,5,6,4,5,6,7,5,6,7,8,6,7,8,9,7,8,9,a,8,9,a,b,9,a
  //   ,b,c,1,2,3,4,2,3,4,5,3,4,5,6,4,5,6,7,5,6,7,8,6,7,8,9,7,8,9,a,8
  //   ,9,a,b,3,4,5,6,4,5,6,7,5,6,7,8,6,7,8,9,7,8,9,a,8,9,a,b,9,a,b,c
  //   ,a,b,c,d,2,3,4,5,3,4,5,6,4,5,6,7,5,6,7,8,6,7,8,9,7,8,9,a,8,9,a
  //   ,b,9,a,b,c,4,5,6,7,5,6,7,8,6,7,8,9,7,8,9,a,8,9,a,b,9,a,b,c,a,b
  //   ,c,d,b,c,d,e,3,4,5,6,4,5,6,7,5,6,7,8,6,7,8,9,7,8,9,a,8,9,a,b,9
  //   ,a,b,c,a,b,c,d,5,6,7,8,6,7,8,9,7,8,9,a,8,9,a,b,9,a,b,c,a,b,c,d
  //   ,b,c,d,e,c,d,e,f,1,2,3,4,2,3,4,5,3,4,5,6,4,5,6,7,5,6,7,8,6,7,8
  //   ,9,7,8,9,a,8,9,a,b,3,4,5,6,4,5,6,7,5,6,7,8,6,7,8,9,7,8,9,a,8,9
  //   ,a,b,9,a,b,c,a,b,c,d,2,3,4,5,3,4,5,6,4,5,6,7,5,6,7,8,6,7,8,9,7
  //   ,8,9,a,8,9,a,b,9,a,b,c,4,5,6,7,5,6,7,8,6,7,8,9,7,8,9,a,8,9,a,b
  //   ,9,a,b,c,a,b,c,d,b,c,d,e,3,4,5,6,4,5,6,7,5,6,7,8,6,7,8,9,7,8,9
  //   ,a,8,9,a,b,9,a,b,c,a,b,c,d,5,6,7,8,6,7,8,9,7,8,9,a,8,9,a,b,9,a
  //   ,b,c,a,b,c,d,b,c,d,e,c,d,e,f,4,5,6,7,5,6,7,8,6,7,8,9,7,8,9,a,8
  //   ,9,a,b,9,a,b,c,a,b,c,d,b,c,d,e,6,7,8,9,7,8,9,a,8,9,a,b,9,a,b,c
  //   ,a,b,c,d,b,c,d,e,c,d,e,f,d,e,f,10
  //   contents of Kernel_7 (hex, n*v repeats v):
  //   0,1,2,3,1,2,3,4,2,3,4,5,3,4,5,6,4,5,6,7,5,6,7,8,6,7,8,9,7,8,9
  //   ,a,2,3,4,5,3,4,5,6,4,5,6,7,5,6,7,8,6,7,8,9,7,8,9,a,8,9,a,b,9,a
  //   ,b,c,1,2,3,4,2,3,4,5,3,4,5,6,4,5,6,7,5,6,7,8,6,7,8,9,7,8,9,a,8
  //   ,9,a,b,3,4,5,6,4,5,6,7,5,6,7,8,6,7,8,9,7,8,9,a,8,9,a,b,9,a,b,c
  //   ,a,b,c,d,2,3,4,5,3,4,5,6,4,5,6,7,5,6,7,8,6,7,8,9,7,8,9,a,8,9,a
  //   ,b,9,a,b,c,4,5,6,7,5,6,7,8,6,7,8,9,7,8,9,a,8,9,a,b,9,a,b,c,a,b
  //   ,c,d,b,c,d,e,3,4,5,6,4,5,6,7,5,6,7,8,6,7,8,9,7,8,9,a,8,9,a,b,9
  //   ,a,b,c,a,b,c,d,5,6,7,8,6,7,8,9,7,8,9,a,8,9,a,b,9,a,b,c,a,b,c,d
  //   ,b,c,d,e,c,d,e,f,1,2,3,4,2,3,4,5,3,4,5,6,4,5,6,7,5,6,7,8,6,7,8
  //   ,9,7,8,9,a,8,9,a,b,3,4,5,6,4,5,6,7,5,6,7,8,6,7,8,9,7,8,9,a,8,9
  //   ,a,b,9,a,b,c,a,b,c,d,2,3,4,5,3,4,5,6,4,5,6,7,5,6,7,8,6,7,8,9,7
  //   ,8,9,a,8,9,a,b,9,a,b,c,4,5,6,7,5,6,7,8,6,7,8,9,7,8,9,a,8,9,a,b
  //   ,9,a,b,c,a,b,c,d,b,c,d,e,3,4,5,6,4,5,6,7,5,6,7,8,6,7,8,9,7,8,9
  //   ,a,8,9,a,b,9,a,b,c,a,b,c,d,5,6,7,8,6,7,8,9,7,8,9,a,8,9,a,b,9,a
  //   ,b,c,a,b,c,d,b,c,d,e,c,d,e,f,4,5,6,7,5,6,7,8,6,7,8,9,7,8,9,a,8
  //   ,9,a,b,9,a,b,c,a,b,c,d,b,c,d,e,6,7,8,9,7,8,9,a,8,9,a,b,9,a,b,c
  //   ,a,b,c,d,b,c,d,e,c,d,e,f,d,e,f,10
  //   contents of Kernel_8 (hex, n*v repeats v):
  //   0,1,2,3,1,2,3,4,2,3,4,5,3,4,5,6,4,5,6,7,5,6,7,8,6,7,8,9,7,8,9
  //   ,a,2,3,4,5,3,4,5,6,4,5,6,7,5,6,7,8,6,7,8,9,7,8,9,a,8,9,a,b,9,a
  //   ,b,c,1,2,3,4,2,3,4,5,3,4,5,6,4,5,6,7,5,6,7,8,6,7,8,9,7,8,9,a,8
  //   ,9,a,b,3,4,5,6,4,5,6,7,5,6,7,8,6,7,8,9,7,8,9,a,8,9,a,b,9,a,b,c
  //   ,a,b,c,d,2,3,4,5,3,4,5,6,4,5,6,7,5,6,7,8,6,7,8,9,7,8,9,a,8,9,a
  //   ,b,9,a,b,c,4,5,6,7,5,6,7,8,6,7,8,9,7,8,9,a,8,9,a,b,9,a,b,c,a,b
  //   ,c,d,b,c,d,e,3,4,5,6,4,5,6,7,5,6,7,8,6,7,8,9,7,8,9,a,8,9,a,b,9
  //   ,a,b,c,a,b,c,d,5,6,7,8,6,7,8,9,7,8,9,a,8,9,a,b,9,a,b,c,a,b,c,d
  //   ,b,c,d,e,c,d,e,f,1,2,3,4,2,3,4,5,3,4,5,6,4,5,6,7,5,6,7,8,6,7,8
  //   ,9,7,8,9,a,8,9,a,b,3,4,5,6,4,5,6,7,5,6,7,8,6,7,8,9,7,8,9,a,8,9
  //   ,a,b,9,a,b,c,a,b,c,d,2,3,4,5,3,4,5,6,4,5,6,7,5,6,7,8,6,7,8,9,7
  //   ,8,9,a,8,9,a,b,9,a,b,c,4,5,6,7,5,6,7,8,6,7,8,9,7,8,9,a,8,9,a,b
  //   ,9,a,b,c,a,b,c,d,b,c,d,e,3,4,5,6,4,5,6,7,5,6,7,8,6,7,8,9,7,8,9
  //   ,a,8,9,a,b,9,a,b,c,a,b,c,d,5,6,7,8,6,7,8,9,7,8,9,a,8,9,a,b,9,a
  //   ,b,c,a,b,c,d,b,c,d,e,c,d,e,f,4,5,6,7,5,6,7,8,6,7,8,9,7,8,9,a,8
  //   ,9,a,b,9,a,b,c,a,b,c,d,b,c,d,e,6,7,8,9,7,8,9,a,8,9,a,b,9,a,b,c
  //   ,a,b,c,d,b,c,d,e,c,d,e,f,d,e,f,10
endmodule
