// Digital circuit TreeCNN.dig as structural Verilog
module TreeCNN (
  input  [7:0] w46,
  input  [7:0] w47,
  input  [7:0] w48,
  input  [7:0] w49,
  input  [7:0] w50,
  input  [7:0] w51,
  input  [7:0] w52,
  input  [7:0] w53,
  input  [7:0] w54,
  input  [7:0] w55,
  input  [7:0] w56,
  input  [7:0] w57,
  input  [7:0] w58,
  input  [7:0] w59,
  input  [7:0] w60,
  input  [7:0] w61,
  input  [7:0] w62,
  input  [7:0] w63,
  output [23:0] out_1,
  output [11:0] out_11
);

  wire _5bittcbsdconvcesion_1_p2, _5bittcbsdconvcesion_2_p2, _5bittcbsdconvcesion_3_p3,
       _5bittcbsdconvcesion_4_p2;
  wire [4:0] parralelromgaussian_1_out0, parralelromgaussian_1_out1, parralelromgaussian_1_out2,
       parralelromgaussian_1_out3, parralelromgaussian_1_out4, parralelromgaussian_1_out5,
       parralelromgaussian_1_out6, parralelromgaussian_1_out7, parralelromgaussian_2_out0,
       parralelromgaussian_2_out1, parralelromgaussian_2_out2, parralelromgaussian_2_out3,
       parralelromgaussian_2_out4, parralelromgaussian_2_out5, parralelromgaussian_2_out6,
       parralelromgaussian_2_out7;
  wire [5:0] add_1_s, add_3_s, add_5_s, add_7_s, barrelshifter_1_out, barrelshifter_3_out,
       barrelshifter_4_out, barrelshifter_7_out, bitextender_1_out, bitextender_2_out, bitextender_4_out,
       bitextender_6_out, bitextender_7_out, bitextender_9_out, bitextender_10_out, bitextender_11_out,
       bitextender_13_out, bitextender_15_out, bitextender_16_out, bitextender_18_out;
  wire [7:0] add_2_s, add_6_s, barrelshifter_2_out, barrelshifter_6_out, bitextender_3_out,
       bitextender_8_out, bitextender_12_out, bitextender_17_out;
  wire [8:0] verteiler_1_o0, verteiler_1_o1, verteiler_1_o2, verteiler_1_o3, verteiler_1_o4, verteiler_1_o5,
       verteiler_1_o6, verteiler_1_o7, verteiler_2_o0, verteiler_2_o1, verteiler_2_o2, verteiler_2_o3,
       verteiler_2_o4, verteiler_2_o5, verteiler_2_o6, verteiler_2_o7;
  wire [11:0] _6bitbcdtc_1_bsdout, _6bitbcdtc_2_bsdout, _6bitbcdtc_3_bsdout, _6bitbcdtc_4_bsdout,
       _10to12_1_p2, _10to12_2_p2, _10to12_3_p2, _10to12_4_p2, barrelshifter_5_out, bitextender_5_out,
       bitextender_14_out;
  wire [15:0] _8bitbsdadder_1_out, _8bitbsdadder_2_out, _12to16_1_out, _12to16_2_out, _12to16erw_1_out,
       _12to16erw_2_out;
  wire [23:0] _16to24_1_out, _16to24erw_1_out;

  Verteiler verteiler_1 (
    .w0(w46), .w1(w47), .w2(w48), .w3(w49), .w4(w50), .w5(w51), .w6(w52), .w7(w53), .w8(w54),
    .o0(verteiler_1_o0), .o1(verteiler_1_o1), .o2(verteiler_1_o2), .o3(verteiler_1_o3), .o4(verteiler_1_o4),
    .o5(verteiler_1_o5), .o6(verteiler_1_o6), .o7(verteiler_1_o7));
  Verteiler verteiler_2 (
    .w0(w55), .w1(w56), .w2(w57), .w3(w58), .w4(w59), .w5(w60), .w6(w61), .w7(w62), .w8(w63),
    .o0(verteiler_2_o0), .o1(verteiler_2_o1), .o2(verteiler_2_o2), .o3(verteiler_2_o3), .o4(verteiler_2_o4),
    .o5(verteiler_2_o5), .o6(verteiler_2_o6), .o7(verteiler_2_o7));
  ParralelRomGaussian parralelromgaussian_1 (
    .in0(verteiler_1_o0), .in1(verteiler_1_o1), .in2(verteiler_1_o2), .in3(verteiler_1_o3),
    .in4(verteiler_1_o4), .in5(verteiler_1_o5), .in6(verteiler_1_o6), .in7(verteiler_1_o7),
    .out0(parralelromgaussian_1_out0), .out1(parralelromgaussian_1_out1), .out2(parralelromgaussian_1_out2),
    .out3(parralelromgaussian_1_out3), .out4(parralelromgaussian_1_out4), .out5(parralelromgaussian_1_out5),
    .out6(parralelromgaussian_1_out6), .out7(parralelromgaussian_1_out7));
  ParralelRomGaussian parralelromgaussian_2 (
    .in0(verteiler_2_o0), .in1(verteiler_2_o1), .in2(verteiler_2_o2), .in3(verteiler_2_o3),
    .in4(verteiler_2_o4), .in5(verteiler_2_o5), .in6(verteiler_2_o6), .in7(verteiler_2_o7),
    .out0(parralelromgaussian_2_out0), .out1(parralelromgaussian_2_out1), .out2(parralelromgaussian_2_out2),
    .out3(parralelromgaussian_2_out3), .out4(parralelromgaussian_2_out4), .out5(parralelromgaussian_2_out5),
    .out6(parralelromgaussian_2_out6), .out7(parralelromgaussian_2_out7));
  BitExtender #(.inputBits(5), .outputBits(6)) bitextender_1 (.in(parralelromgaussian_1_out0), .out(bitextender_1_out));
  BitExtender #(.inputBits(5), .outputBits(6)) bitextender_2 (.in(parralelromgaussian_2_out0), .out(bitextender_2_out));
  _6BitBCDTC _6bitbcdtc_1 (
    .inTC(bitextender_1_out), .inBSD(_10to12_1_p2), .bsdOut(_6bitbcdtc_1_bsdout));  // open: carryOut
  _12To16Erw _12to16erw_1 (.in(_6bitbcdtc_1_bsdout), .out(_12to16erw_1_out));
  Add #(.Bits(6)) add_1 (.a(barrelshifter_1_out), .b(bitextender_2_out), .c_i(1'b0), .s(add_1_s));  // open: c_o
  BitExtender #(.inputBits(6), .outputBits(8)) bitextender_3 (.in(add_1_s), .out(bitextender_3_out));
  // _5BitTCBSDConvcesion _5bittcbsdconvcesion_1: pin names not known; wires that end beside it: parralelromgaussian_1_out1, _5bittcbsdconvcesion_1_p2
  // _10to12 _10to12_1: pin names not known; wires that end beside it: _5bittcbsdconvcesion_1_p2, _10to12_1_p2
  BitExtender #(.inputBits(5), .outputBits(6)) bitextender_4 (.in(parralelromgaussian_2_out1), .out(bitextender_4_out));
  BarrelShifter #(.Bits(6)) barrelshifter_1 (.in(bitextender_4_out), .shift(3'b001), .out(barrelshifter_1_out));
  _8BitBSDAdder _8bitbsdadder_1 (.inA(_12to16_1_out), .inB(_12to16erw_1_out), .out(_8bitbsdadder_1_out));  // open: c
  _16to24Erw _16to24erw_1 (.in(_8bitbsdadder_1_out), .out(_16to24erw_1_out));
  Add #(.Bits(8)) add_2 (.a(barrelshifter_2_out), .b(bitextender_3_out), .c_i(1'b0), .s(add_2_s));  // open: c_o
  BitExtender #(.outputBits(12)) bitextender_5 (.in(add_2_s), .out(bitextender_5_out));
  BitExtender #(.inputBits(5), .outputBits(6)) bitextender_6 (.in(parralelromgaussian_1_out2), .out(bitextender_6_out));
  _12to16 _12to16_1 (.in(_6bitbcdtc_2_bsdout), .out(_12to16_1_out));
  BitExtender #(.inputBits(5), .outputBits(6)) bitextender_7 (.in(parralelromgaussian_2_out2), .out(bitextender_7_out));
  BitExtender #(.inputBits(6), .outputBits(8)) bitextender_8 (.in(add_3_s), .out(bitextender_8_out));
  BarrelShifter #(.Bits(8)) barrelshifter_2 (.in(bitextender_8_out), .shift(4'b0010), .out(barrelshifter_2_out));
  Add #(.Bits(6)) add_3 (.a(barrelshifter_3_out), .b(bitextender_7_out), .c_i(1'b0), .s(add_3_s));  // open: c_o
  _6BitBCDTC _6bitbcdtc_2 (
    .inTC(bitextender_6_out), .inBSD(_10to12_2_p2), .bsdOut(_6bitbcdtc_2_bsdout));  // open: carryOut
  // _5BitTCBSDConvcesion _5bittcbsdconvcesion_2: pin names not known; wires that end beside it: parralelromgaussian_1_out3, _5bittcbsdconvcesion_2_p2
  // _10to12 _10to12_2: pin names not known; wires that end beside it: _5bittcbsdconvcesion_2_p2, _10to12_2_p2
  BitExtender #(.inputBits(5), .outputBits(6)) bitextender_9 (.in(parralelromgaussian_2_out3), .out(bitextender_9_out));
  BarrelShifter #(.Bits(6)) barrelshifter_3 (.in(bitextender_9_out), .shift(3'b001), .out(barrelshifter_3_out));
  BitExtender #(.inputBits(5), .outputBits(6)) bitextender_10 (
    .in(parralelromgaussian_1_out4), .out(bitextender_10_out));
  _12BitBSDAdder _12bitbsdadder_1 (.inA(_16to24_1_out), .inB(_16to24erw_1_out), .out(out_1));  // open: carry
  BitExtender #(.inputBits(5), .outputBits(6)) bitextender_11 (
    .in(parralelromgaussian_2_out4), .out(bitextender_11_out));
  Add #(.Bits(12)) add_4 (.a(barrelshifter_5_out), .b(bitextender_5_out), .c_i(1'b0), .s(out_11));  // open: c_o
  Add #(.Bits(6)) add_5 (.a(barrelshifter_4_out), .b(bitextender_11_out), .c_i(1'b0), .s(add_5_s));  // open: c_o
  BitExtender #(.inputBits(6), .outputBits(8)) bitextender_12 (.in(add_5_s), .out(bitextender_12_out));
  _6BitBCDTC _6bitbcdtc_3 (
    .inTC(bitextender_10_out), .inBSD(_10to12_3_p2), .bsdOut(_6bitbcdtc_3_bsdout));  // open: carryOut
  _12To16Erw _12to16erw_2 (.in(_6bitbcdtc_3_bsdout), .out(_12to16erw_2_out));
  // _5BitTCBSDConvcesion _5bittcbsdconvcesion_3: pin names not known; wires that end beside it: parralelromgaussian_1_out4, parralelromgaussian_1_out5, _5bittcbsdconvcesion_3_p3, parralelromgaussian_1_out5
  // _10to12 _10to12_3: pin names not known; wires that end beside it: _5bittcbsdconvcesion_3_p3, _10to12_3_p2
  BitExtender #(.inputBits(5), .outputBits(6)) bitextender_13 (
    .in(parralelromgaussian_2_out5), .out(bitextender_13_out));
  BarrelShifter #(.Bits(6)) barrelshifter_4 (.in(bitextender_13_out), .shift(3'b001), .out(barrelshifter_4_out));
  BitExtender #(.outputBits(12)) bitextender_14 (.in(add_6_s), .out(bitextender_14_out));
  BarrelShifter #(.Bits(12)) barrelshifter_5 (.in(bitextender_14_out), .shift(4'b0100), .out(barrelshifter_5_out));
  _16to24 _16to24_1 (.in(_8bitbsdadder_2_out), .out(_16to24_1_out));
  Add #(.Bits(8)) add_6 (.a(barrelshifter_6_out), .b(bitextender_12_out), .c_i(1'b0), .s(add_6_s));  // open: c_o
  BitExtender #(.inputBits(5), .outputBits(6)) bitextender_15 (
    .in(parralelromgaussian_1_out6), .out(bitextender_15_out));
  _8BitBSDAdder _8bitbsdadder_2 (.inA(_12to16_2_out), .inB(_12to16erw_2_out), .out(_8bitbsdadder_2_out));  // open: c
  BitExtender #(.inputBits(5), .outputBits(6)) bitextender_16 (
    .in(parralelromgaussian_2_out6), .out(bitextender_16_out));
  _12to16 _12to16_2 (.in(_6bitbcdtc_4_bsdout), .out(_12to16_2_out));
  BitExtender #(.inputBits(6), .outputBits(8)) bitextender_17 (.in(add_7_s), .out(bitextender_17_out));
  BarrelShifter #(.Bits(8)) barrelshifter_6 (.in(bitextender_17_out), .shift(4'b0010), .out(barrelshifter_6_out));
  _6BitBCDTC _6bitbcdtc_4 (
    .inTC(bitextender_15_out), .inBSD(_10to12_4_p2), .bsdOut(_6bitbcdtc_4_bsdout));  // open: carryOut
  Add #(.Bits(6)) add_7 (.a(barrelshifter_7_out), .b(bitextender_16_out), .c_i(1'b0), .s(add_7_s));  // open: c_o
  BitExtender #(.inputBits(5), .outputBits(6)) bitextender_18 (
    .in(parralelromgaussian_2_out7), .out(bitextender_18_out));
  BarrelShifter #(.Bits(6)) barrelshifter_7 (.in(bitextender_18_out), .shift(3'b001), .out(barrelshifter_7_out));
  // _5BitTCBSDConvcesion _5bittcbsdconvcesion_4: pin names not known; wires that end beside it: parralelromgaussian_1_out7, _5bittcbsdconvcesion_4_p2
  // _10to12 _10to12_4: pin names not known; wires that end beside it: _5bittcbsdconvcesion_4_p2, _10to12_4_p2

  // Notes on the sheet:
  //   Minimal Gaussian Filter mit:
  //   1 2 1 
  //   2 4 2
  //   1 2 1
  //   => maximaler wert im ROM:
  //   0b1111 => 1+2+1+2+4+2+1+2+1 = 16 => 5bit
  //   auf 512 adressen
  //   => level1 : 6bit adder 
  //   => level2 : 8bit adder
  //   => level3 : 12 bit adder
  //   im Rom liegen TC werte
  //   5
  //   5bit
  //   6bit Adder (BCD TC)
  //   6 bit(12 BSD)
  //   10
  //   12
  //   8bitAdder(BCD BCD)
  //   8Bit BSD
  //   12bit
  //   6bit (12BSD)
  //   12bit Adder (BCD BCD)
  //   16bit
endmodule
