// Digital circuit Verteiler.dig as structural Verilog
module Verteiler (
  input  [7:0] w0,
  input  [7:0] w1,
  input  [7:0] w2,
  input  [7:0] w3,
  input  [7:0] w4,
  input  [7:0] w5,
  input  [7:0] w6,
  input  [7:0] w7,
  input  [7:0] w8,
  output [8:0] o0,
  output [8:0] o1,
  output [8:0] o2,
  output [8:0] o3,
  output [8:0] o4,
  output [8:0] o5,
  output [8:0] o6,
  output [8:0] o7
);


  assign o0 = {w0[0], w1[0], w2[0], w3[0], w4[0], w5[0], w6[0], w7[0], w8[0]};
  assign o1 = {w0[1], w1[1], w2[1], w3[1], w4[1], w5[1], w6[1], w7[1], w8[1]};
  assign o2 = {w0[2], w1[2], w2[2], w3[2], w4[2], w5[2], w6[2], w7[2], w8[2]};
  assign o3 = {w0[3], w1[3], w2[3], w3[3], w4[3], w5[3], w6[3], w7[3], w8[3]};
  assign o4 = {w0[4], w1[4], w2[4], w3[4], w4[4], w5[4], w6[4], w7[4], w8[4]};
  assign o5 = {w0[5], w1[5], w2[5], w3[5], w4[5], w5[5], w6[5], w7[5], w8[5]};
  assign o6 = {w0[6], w1[6], w2[6], w3[6], w4[6], w5[6], w6[6], w7[6], w8[6]};
  assign o7 = {w0[7], w1[7], w2[7], w3[7], w4[7], w5[7], w6[7], w7[7], w8[7]};

  // Other names for the same wires on the sheet: t1 = w0[0]; t2 = w0[1]; t3 = w0[2]; t4 = w0[3]; t5 = w0[4];
  //   t6 = w0[5]; t7 = w0[6]; t8 = w0[7]; a1 = w1[0]; a2 = w1[1]; a3 = w1[2]; a4 = w1[3]; a5 = w1[4]; a6 = w1[5];
  //   a7 = w1[6]; a8 = w1[7]; b1 = w2[0]; b2 = w2[1]; b3 = w2[2]; b4 = w2[3]; b5 = w2[4]; b6 = w2[5]; b7 = w2[6];
  //   b8 = w2[7]; c1 = w3[0]; c2 = w3[1]; c3 = w3[2]; c4 = w3[3]; c5 = w3[4]; c6 = w3[5]; c7 = w3[6]; c8 = w3[7];
  //   d1 = w4[0]; d2 = w4[1]; d3 = w4[2]; d4 = w4[3]; d5 = w4[4]; d6 = w4[5]; d7 = w4[6]; d8 = w4[7]; e1 = w5[0];
  //   e2 = w5[1]; e3 = w5[2]; e4 = w5[3]; e5 = w5[4]; e6 = w5[5]; e7 = w5[6]; e8 = w5[7]; f1 = w6[0]; f2 = w6[1];
  //   f3 = w6[2]; f4 = w6[3]; f5 = w6[4]; f6 = w6[5]; f7 = w6[6]; f8 = w6[7]; g1 = w7[0]; g2 = w7[1]; g3 = w7[2];
  //   g4 = w7[3]; g5 = w7[4]; g6 = w7[5]; g7 = w7[6]; g8 = w7[7]; h1 = w8[0]; h2 = w8[1]; h3 = w8[2]; h4 = w8[3];
  //   h5 = w8[4]; h6 = w8[5]; h7 = w8[6]; h8 = w8[7]
endmodule
