// Logisim project 4BitBSDAdder.circ as structural Verilog: 6 circuits, main circuit main
module main (
  input  [15:0] in_1,
  input  [15:0] in_2,
  output [15:0] out_3,
  output [1:0] out_4
);

  wire adder_1_cout, adder_1_out, adder_2_cout, adder_2_out, adder_3_cout, adder_3_out, adder_4_cout,
       adder_4_out, adder_5_cout, adder_5_out, adder_6_cout, adder_6_out, adder_7_cout, adder_7_out,
       adder_8_out;

  Adder #(.width(1)) adder_1 (.a(in_1[0]), .b(in_2[0]), .out(adder_1_out), .cin(in_1[1]), .cout(adder_1_cout));
  Adder #(.width(1)) adder_2 (.a(in_1[2]), .b(in_2[2]), .out(adder_2_out), .cin(in_1[3]), .cout(adder_2_cout));
  Adder #(.width(1)) adder_3 (.a(in_1[4]), .b(in_2[4]), .out(adder_3_out), .cin(in_1[5]), .cout(adder_3_cout));
  Adder #(.width(1)) adder_4 (.a(in_1[6]), .b(in_2[6]), .out(adder_4_out), .cin(in_1[7]), .cout(adder_4_cout));
  Adder #(.width(1)) adder_5 (.a(in_1[8]), .b(in_2[8]), .out(adder_5_out), .cin(in_1[9]), .cout(adder_5_cout));
  Adder #(.width(1)) adder_6 (.a(in_1[10]), .b(in_2[10]), .out(adder_6_out), .cin(in_1[11]), .cout(adder_6_cout));
  Adder #(.width(1)) adder_7 (.a(in_1[12]), .b(in_2[12]), .out(adder_7_out), .cin(in_1[13]), .cout(adder_7_cout));
  Adder #(.width(1)) adder_8 (.a(in_1[14]), .b(in_2[14]), .out(adder_8_out), .cin(in_1[15]), .cout(out_4[1]));
  Adder #(.width(1)) adder_9 (.a(1'b1), .b(adder_1_out), .out(out_3[1]), .cin(in_2[1]), .cout(out_3[2]));
  Adder #(.width(1)) adder_10 (.a(adder_1_cout), .b(adder_2_out), .out(out_3[3]), .cin(in_2[3]), .cout(out_3[4]));
  Adder #(.width(1)) adder_11 (.a(adder_2_cout), .b(adder_3_out), .out(out_3[5]), .cin(in_2[5]), .cout(out_3[6]));
  Adder #(.width(1)) adder_12 (.a(adder_3_cout), .b(adder_4_out), .out(out_3[7]), .cin(in_2[7]), .cout(out_3[8]));
  Adder #(.width(1)) adder_13 (.a(adder_4_cout), .b(adder_5_out), .out(out_3[9]), .cin(in_2[9]), .cout(out_3[10]));
  Adder #(.width(1)) adder_14 (.a(adder_5_cout), .b(adder_6_out), .out(out_3[11]), .cin(in_2[11]), .cout(out_3[12]));
  Adder #(.width(1)) adder_15 (.a(adder_6_cout), .b(adder_7_out), .out(out_3[13]), .cin(in_2[13]), .cout(out_3[14]));
  Adder #(.width(1)) adder_16 (.a(adder_7_cout), .b(adder_8_out), .out(out_3[15]), .cin(in_2[15]), .cout(out_4[0]));

  assign out_3[0] = 1'b0;

  // Other names for the same wires on the sheet: A0a = in_1[0]; A0b = in_1[1]; A1a = in_1[2]; A1b = in_1[3];
  //   A2a = in_1[4]; A2b = in_1[5]; A3a = in_1[6]; A3b = in_1[7]; A4a = in_1[8]; A4b = in_1[9]; A5a = in_1[10];
  //   A5b = in_1[11]; A6a = in_1[12]; A6b = in_1[13]; A7a = in_1[14]; A7b = in_1[15]; B0a = in_2[0]; B0b = in_2[1];
  //   B1a = in_2[2]; B1b = in_2[3]; B2a = in_2[4]; B2b = in_2[5]; B3a = in_2[6]; B3b = in_2[7]; B4a = in_2[8];
  //   B4b = in_2[9]; B5a = in_2[10]; B5b = in_2[11]; B6a = in_2[12]; B6b = in_2[13]; B7a = in_2[14]; B7b = in_2[15]

  // Notes on the sheet:
  //   overflow
endmodule

module Mul (
  input  [7:0] in_1,
  input  [7:0] in_2,
  output [15:0] out_3,
  output [1:0] overflow,
  output [15:0] out_5
);

  wire [1:0] main_1_out_4, main_2_out_4, main_3_out_4;
  wire [15:0] bsdshifter_1_out_2, bsdshifter_2_out_2, main_1_out_3, main_2_out_3, main_3_out_3, minus_w,
       multiplexer_1_out, multiplexer_2_out, multiplexer_3_out, multiplexer_4_out, not_2_out, not_3_out,
       not_4_out, not_5_out;

  assign minus_w = ~{8'h55, in_2};  // NOT_Gate not_1, 16 bits wide
  bsdShifter bsdshifter_1 (.in_1(bsdshifter_2_out_2), .out_2(bsdshifter_1_out_2));
  assign not_2_out = ~{8'h55, in_2};  // NOT_Gate not_2, 16 bits wide
  assign not_3_out = ~bsdshifter_1_out_2;  // NOT_Gate not_3, 16 bits wide
  Multiplexer #(.select(2), .width(16), .enable("false")) multiplexer_1 (
    .in0(not_2_out), .in1(16'h5555), .in2(16'h5555), .in3({8'h55, in_2}), .out(multiplexer_1_out),
    .sel({in_1[0], in_1[1]}));
  Multiplexer #(.select(2), .width(16), .enable("false")) multiplexer_2 (
    .in0(not_3_out), .in1(16'h5555), .in2(16'h5555), .in3(bsdshifter_1_out_2), .out(multiplexer_2_out),
    .sel({in_1[4], in_1[5]}));
  main main_1 (.in_1(multiplexer_1_out), .in_2(16'h5555), .out_3(main_1_out_3), .out_4(main_1_out_4));
  main main_2 (.in_1(multiplexer_2_out), .in_2(main_3_out_3), .out_3(main_2_out_3), .out_4(main_2_out_4));
  bsdShifter bsdshifter_2 (.in_1({8'h55, in_2}), .out_2(bsdshifter_2_out_2));
  bsdShifter bsdshifter_3 (.in_1(bsdshifter_1_out_2), .out_2(out_3));
  assign not_4_out = ~bsdshifter_2_out_2;  // NOT_Gate not_4, 16 bits wide
  assign not_5_out = ~out_3;  // NOT_Gate not_5, 16 bits wide
  Multiplexer #(.select(2), .width(16), .enable("false")) multiplexer_3 (
    .in0(not_4_out), .in1(16'h5555), .in2(16'h5555), .in3(bsdshifter_2_out_2), .out(multiplexer_3_out),
    .sel({in_1[2], in_1[3]}));
  Multiplexer #(.select(2), .width(16), .enable("false")) multiplexer_4 (
    .in0(not_5_out), .in1(16'h5555), .in2(16'h5555), .in3(out_3), .out(multiplexer_4_out),
    .sel({in_1[6], in_1[7]}));
  main main_3 (.in_1(multiplexer_3_out), .in_2(main_1_out_3), .out_3(main_3_out_3), .out_4(main_3_out_4));
  main main_4 (.in_1(multiplexer_4_out), .in_2(main_2_out_3), .out_3(out_5), .out_4(overflow));

  // Other names for the same wires on the sheet: A2b = in_1[5]; A2a = in_1[4]; A0b = in_1[1]; A0a = in_1[0];
  //   A1b = in_1[3]; A1a = in_1[2]; A3b = in_1[7]; A3a = in_1[6]; w[7:0] = in_2

  // Notes on the sheet:
  //   A
  //   B
  //   Zero leitung
  //   overflow
  //   res nach erstem add
  //   overflow
  //   res nach erstem add
  //   res nach left shift
  //   res nach left shift
  //   acc
  //   acc
  //   overflow
  //   res nach erstem add
  //   res nach erstem add
  //   res nach left shift
  //   res nach left shift
  //   acc
  //   acc
  //   Res
endmodule

module bsdShifter (
  input  [15:0] in_1,
  output [15:0] out_2
);


  assign out_2 = {in_1[13:0], 2'b01};
endmodule

module bsdtoBinConveter (
  input  [15:0] in_1,
  output [7:0] out_2
);

  wire or_1_out, or_2_out, or_3_out, or_4_out, or_5_out, or_6_out, or_7_out, or_8_out, subtractor_1_bout;
  wire [7:0] and_1_out, not_7_out;

  and and_1 (and_1_out[0], in_1[0], in_1[1]);
  and and_2 (and_1_out[1], in_1[2], in_1[3]);
  and and_3 (and_1_out[2], in_1[4], in_1[5]);
  and and_4 (and_1_out[3], in_1[6], in_1[7]);
  and and_5 (and_1_out[4], in_1[8], in_1[9]);
  and and_6 (and_1_out[5], in_1[10], in_1[11]);
  and and_7 (and_1_out[6], in_1[12], in_1[13]);
  and and_8 (and_1_out[7], in_1[14], in_1[15]);
  or or_1 (or_1_out, in_1[0], in_1[1]);
  or or_2 (or_2_out, in_1[2], in_1[3]);
  or or_3 (or_3_out, in_1[4], in_1[5]);
  not not_1 (not_7_out[2], or_3_out);
  or or_4 (or_4_out, in_1[6], in_1[7]);
  not not_2 (not_7_out[3], or_4_out);
  or or_5 (or_5_out, in_1[8], in_1[9]);
  not not_3 (not_7_out[4], or_5_out);
  not not_4 (not_7_out[5], or_6_out);
  or or_6 (or_6_out, in_1[10], in_1[11]);
  not not_5 (not_7_out[6], or_7_out);
  or or_7 (or_7_out, in_1[12], in_1[13]);
  or or_8 (or_8_out, in_1[14], in_1[15]);
  not not_6 (not_7_out[7], or_8_out);
  not not_7 (not_7_out[0], or_1_out);
  not not_8 (not_7_out[1], or_2_out);
  Subtractor subtractor_1 (.a(and_1_out), .b(not_7_out), .out(out_2), .bout(subtractor_1_bout));  // open: bin

  // Notes on the sheet:
  //   pi
  //   ni
  //   pi
  //   ni
  //   pi
  //   ni
  //   pi
  //   ni
  //   pi
  //   ni
  //   pi
  //   ni
  //   pi
  //   ni
  //   pi
  //   ni
  //   neg
  //   pos
  //   P-N
  //   overflow
endmodule

module bintoBSDconv (
  input  [3:0] in_1,
  output [7:0] out_2
);


  assign out_2 = {1'b1, in_1[3], 1'b1, in_1[2], 1'b1, in_1[1], 1'b1, in_1[0]};
endmodule

module test (
  input  [3:0] in_1,
  input  [3:0] in_2,
  input  [7:0] in_3,
  input  [7:0] in_4,
  output [7:0] out_5,
  output [1:0] out_6,
  output [15:0] out_7
);

  wire [7:0] bintobsdconv_1_out_2, bintobsdconv_2_out_2;
  wire [15:0] mul_1_overflow;

  Hex_Digit_Display hex_digit_display_1 (.value(in_1));  // open: dp
  Hex_Digit_Display hex_digit_display_2 (.value(in_2));  // open: dp
  bintoBSDconv bintobsdconv_1 (.in_1(in_1), .out_2(bintobsdconv_1_out_2));
  bintoBSDconv bintobsdconv_2 (.in_1(in_2), .out_2(bintobsdconv_2_out_2));
  Mul mul_1 (
    .in_1(bintobsdconv_1_out_2), .in_2(bintobsdconv_2_out_2), .overflow(mul_1_overflow[1:0]));  // open: out_3, out_5
  // Mul mul_2: pin names not known; wires that end beside it: in_3, in_4, out_6, out_7
  bsdtoBinConveter bsdtobinconveter_1 (.in_1(mul_1_overflow), .out_2(out_5));
  Hex_Digit_Display hex_digit_display_3 (.value(out_5[7:4]));  // open: dp
  Hex_Digit_Display hex_digit_display_4 (.value(out_5[3:0]));  // open: dp
  // Pins of 2 and 16 bits meet at mul_1_overflow

  // Notes on the sheet:
  //   bsd representation
  //   binary representation
  //   x
  //   =
endmodule
