// Digital circuit 4digitTC4digitBSDadder.dig as structural Verilog
module _4digitTC4digitBSDadder (
  input  [7:0] \input ,
  input  [7:0] uio,
  input  clk,
  input  [15:0] input_2,
  input  [7:0] input_3,
  input  [7:0] C_BSD,
  input  [3:0] S_TC,
  input  [7:0] A_BSD,
  input  [3:0] B_TC,
  input  rst,
  output [7:0] outBSD,
  output [11:0] outBSD_2,
  output [19:0] outBSD_3
);

  wire [9:0] _4bbsdtcadder_1_bsdout, _4bbsdtcadder_2_bsdout, bsdtcadderninsigned_1_bsdout;
  wire [9:8] bsdtcadderninsigned_2_bsdout;

  BSDTCadderNinSigned bsdtcadderninsigned_1 (
    .inTC(input_3[7:4]), .inBSD(input_2[15:8]), .bsdOut(bsdtcadderninsigned_1_bsdout));
  _6BSDbitAdder _6bsdbitadder_1 (
    .inA(bsdtcadderninsigned_1_bsdout), .inB(bsdtcadderninsigned_2_bsdout), .out(outBSD_3[19:8]));  // open: i1, i2, i3
  BSDTCadderNinSigned bsdtcadderninsigned_2 (
    .inTC(input_3[3:0]), .inBSD(input_2[7:0]), .bsdOut({bsdtcadderninsigned_2_bsdout, outBSD_3[7:0]}));
  TheAdder theadder_1 (.\input (\input ), .uio(uio), .clk(clk), .rst(rst), .outBSD(outBSD));
  _4bBsdTCAdder _4bbsdtcadder_1 (.inTC(S_TC), .inBSD(C_BSD), .bsdOut(_4bbsdtcadder_1_bsdout));
  _6BitBSD _6bitbsd_1 (.inA(_4bbsdtcadder_2_bsdout), .inB(_4bbsdtcadder_1_bsdout), .out(outBSD_2));
  _4bBsdTCAdder _4bbsdtcadder_2 (.inTC(B_TC), .inBSD(A_BSD), .bsdOut(_4bbsdtcadder_2_bsdout));

  // Notes on the sheet:
  //   uio: tiny tapeout uio[7:0] GPIO
  //   Input BSD [15:0]
  //   Intput TC [7:0]
  //   BSD Splitted in 
  //      [ h4, h3, h2, h1, h0] , [ l4, l3 ,l2, l1, l0 ] BSD jewils 2 phsische bit
  //   + [ h4 ,h3, h2 ,h1 ,h0 ] , [ l4, l3 ,l2, l1, l0 ] TC
  //   Low :   0    0     0     0     0    l4    l3   l2   l1   l0
  //   High:   0    h4   h3   h2   h1   h0   0    0    0    0
  //   l4 +h0 kann aber crit pfad direkt O(1) berechnet werden Druch BSD darstellung 
  //   output BSD [19:0]
  //   sollte theoretisch erstetzbar sein druch eifnacheren incrementer
  //   10Bit Out high
  //   10Bit Out low
  //   (A+B) + (C+D)
endmodule
