// Digital circuit 6BSDbitAdder.dig as structural Verilog
module _6BSDbitAdder (
  input  [9:0] inA,
  input  [1:0] inB,
  output [11:0] out,
  output i1,
  output i2,
  output i3
);

  wire add_1_c_o, add_1_s, add_2_c_o, add_2_s, add_3_c_o, add_3_s, add_4_c_o, add_4_s, add_5_s;

  Add add_1 (.a(inA[0]), .b(inB[0]), .c_i(inA[1]), .s(add_1_s), .c_o(add_1_c_o));
  Add add_2 (.a(inA[2]), .b(1'b1), .c_i(inA[3]), .s(add_2_s), .c_o(add_2_c_o));
  Add add_3 (.a(inA[4]), .b(1'b1), .c_i(inA[5]), .s(add_3_s), .c_o(add_3_c_o));
  Add add_4 (.a(inA[6]), .b(1'b1), .c_i(inA[7]), .s(add_4_s), .c_o(add_4_c_o));
  Add add_5 (.a(inA[8]), .b(1'b1), .c_i(inA[9]), .s(add_5_s), .c_o(out[11]));
  Add add_6 (.a(1'b1), .b(add_1_s), .c_i(inB[1]), .s(out[1]), .c_o(out[2]));
  Add add_7 (.a(add_1_c_o), .b(add_2_s), .c_i(1'b0), .s(out[3]), .c_o(out[4]));
  Add add_8 (.a(add_2_c_o), .b(add_3_s), .c_i(1'b0), .s(out[5]), .c_o(out[6]));
  Add add_9 (.a(add_3_c_o), .b(add_4_s), .c_i(1'b0), .s(out[7]), .c_o(out[8]));
  Add add_10 (.a(add_4_c_o), .b(add_5_s), .c_i(1'b0), .s(out[9]), .c_o(out[10]));
  not not_1 (i1, inA[4]);
  and and_1 (i2, inA[5], inA[4]);
  or or_1 (i3, inA[4], inA[5]);

  assign out[0] = 1'b0;

  // Other names for the same wires on the sheet: _1 = inA[0]; _2 = inA[1]; _3 = inA[2]; _4 = inA[3]; _5 = inA[4];
  //   _6 = inA[5]; _7 = inA[6]; _8 = inA[7]; _9 = inA[8]; _10 = inA[9]; _1b = inB[0]; _2b = inB[1]
endmodule
