// Digital circuit BSDAdder.dig as structural Verilog
module BSDAdder (
  input  [17:0] inA,
  input  [17:0] inB,
  output [17:0] out,
  output [1:0] c
);

  wire add_1_c_o, add_1_s, add_2_c_o, add_2_s, add_3_c_o, add_3_s, add_4_c_o, add_4_s, add_5_c_o, add_5_s,
       add_6_c_o, add_6_s, add_7_c_o, add_7_s, add_8_c_o, add_8_s, add_9_s;

  Add add_1 (.a(inA[0]), .b(inB[0]), .c_i(inA[1]), .s(add_1_s), .c_o(add_1_c_o));
  Add add_2 (.a(inA[2]), .b(inB[2]), .c_i(inA[3]), .s(add_2_s), .c_o(add_2_c_o));
  Add add_3 (.a(inA[4]), .b(inB[4]), .c_i(inA[5]), .s(add_3_s), .c_o(add_3_c_o));
  Add add_4 (.a(inA[6]), .b(inB[6]), .c_i(inA[7]), .s(add_4_s), .c_o(add_4_c_o));
  Add add_5 (.a(inA[8]), .b(inB[8]), .c_i(inA[9]), .s(add_5_s), .c_o(add_5_c_o));
  Add add_6 (.a(inA[10]), .b(inB[10]), .c_i(inA[11]), .s(add_6_s), .c_o(add_6_c_o));
  Add add_7 (.a(inA[12]), .b(inB[12]), .c_i(inA[13]), .s(add_7_s), .c_o(add_7_c_o));
  Add add_8 (.a(inA[14]), .b(inB[14]), .c_i(inA[15]), .s(add_8_s), .c_o(add_8_c_o));
  Add add_9 (.a(inA[16]), .b(inB[16]), .c_i(inA[17]), .s(add_9_s), .c_o(c[1]));
  Add add_10 (.a(1'b1), .b(add_1_s), .c_i(inB[1]), .s(out[1]), .c_o(out[2]));
  Add add_11 (.a(add_1_c_o), .b(add_2_s), .c_i(inB[3]), .s(out[3]), .c_o(out[4]));
  Add add_12 (.a(add_2_c_o), .b(add_3_s), .c_i(inB[5]), .s(out[5]), .c_o(out[6]));
  Add add_13 (.a(add_3_c_o), .b(add_4_s), .c_i(inB[7]), .s(out[7]), .c_o(out[8]));
  Add add_14 (.a(add_4_c_o), .b(add_5_s), .c_i(inB[9]), .s(out[9]), .c_o(out[10]));
  Add add_15 (.a(add_5_c_o), .b(add_6_s), .c_i(inB[11]), .s(out[11]), .c_o(out[12]));
  Add add_16 (.a(add_6_c_o), .b(add_7_s), .c_i(inB[13]), .s(out[13]), .c_o(out[14]));
  Add add_17 (.a(add_7_c_o), .b(add_8_s), .c_i(inB[15]), .s(out[15]), .c_o(out[16]));
  Add add_18 (.a(add_8_c_o), .b(add_9_s), .c_i(inB[17]), .s(out[17]), .c_o(c[0]));

  assign out[0] = 1'b0;

  // Other names for the same wires on the sheet: _1 = inA[0]; _2 = inA[1]; _3 = inA[2]; _4 = inA[3]; _5 = inA[4];
  //   _6 = inA[5]; _7 = inA[6]; _8 = inA[7]; _9 = inA[8]; _10 = inA[9]; _11 = inA[10]; _12 = inA[11]; _13 = inA[12];
  //   _14 = inA[13]; _15 = inA[14]; _16 = inA[15]; _17 = inA[16]; _18 = inA[17]; _1b = inB[0]; _2b = inB[1];
  //   _3b = inB[2]; _4b = inB[3]; _5b = inB[4]; _6b = inB[5]; _7b = inB[6]; _8b = inB[7]; _9b = inB[8]; _10b = inB[9];
  //   _11b = inB[10]; _12b = inB[11]; _13b = inB[12]; _14b = inB[13]; _15b = inB[14]; _16b = inB[15]; _17b = inB[16];
  //   _18b = inB[17]
endmodule
