// Digital circuit Conv2x2TC.dig as structural Verilog
module Conv2x2TC (
  input  clk,
  input  reset,
  input  [7:0] w1,
  input  [7:0] w3,
  input  [7:0] w4,
  input  [7:0] w2,
  output cout,
  output [8:0] res
);

  wire [2:0] counter_1_out;
  wire [3:0] multiplexer_3_out;
  wire [7:0] rom_1_d;
  wire [8:0] add_1_s, barrelshifter_1_out, bitextender_1_out;

  Counter #(.Bits(3)) counter_1 (.en(1'b1), .C(clk), .clr(reset), .out(counter_1_out));  // open: ovf
  Multiplexer #(.Selector_Bits(3)) multiplexer_1 (
    .sel(counter_1_out), .in_0(w1[7]), .in_1(w1[6]), .in_2(w1[5]), .in_3(w1[4]), .in_4(w1[3]), .in_5(w1[2]),
    .in_6(w1[1]), .in_7(w1[0]), .out(multiplexer_3_out[3]));
  Multiplexer #(.Selector_Bits(3)) multiplexer_2 (
    .sel(counter_1_out), .in_0(w3[7]), .in_1(w3[6]), .in_2(w3[5]), .in_3(w3[4]), .in_4(w3[3]), .in_5(w3[2]),
    .in_6(w3[1]), .in_7(w3[0]), .out(multiplexer_3_out[1]));
  Multiplexer #(.Selector_Bits(3)) multiplexer_3 (
    .sel(counter_1_out), .in_0(w2[7]), .in_1(w2[6]), .in_2(w2[5]), .in_3(w2[4]), .in_4(w2[3]), .in_5(w2[2]),
    .in_6(w2[1]), .in_7(w2[0]), .out(multiplexer_3_out[2]));
  Multiplexer #(.Selector_Bits(3)) multiplexer_4 (
    .sel(counter_1_out), .in_0(w4[7]), .in_1(w4[6]), .in_2(w4[5]), .in_3(w4[4]), .in_4(w4[3]), .in_5(w4[2]),
    .in_6(w4[1]), .in_7(w4[0]), .out(multiplexer_3_out[0]));
  Register #(.Bits(9)) register_1 (.D(add_1_s), .C(clk), .en(1'b1), .Q(res));
  ROM #(.AddrBits(4), .Bits(8)) rom_1 (.A(multiplexer_3_out), .sel(1'b1), .D(rom_1_d));
  BitExtender #(.outputBits(9)) bitextender_1 (.in(rom_1_d), .out(bitextender_1_out));
  BarrelShifter #(.Bits(9)) barrelshifter_1 (.in(res), .shift(4'b0001), .out(barrelshifter_1_out));
  Add #(.Bits(9)) add_1 (.a(barrelshifter_1_out), .b(bitextender_1_out), .c_i(1'b0), .s(add_1_s), .c_o(cout));

  // Notes on the sheet:
  //   notmale 2s complement schaltung
  //   mit 8 bit pixel values
  //   => 4 bildpunkten => 16 adressen Rom translation
  //   Pixel1
  //   Allgemeiner fall mit 16 bit adder (für grosse filter)
  //   Pixel2
  //   Pixel4
  //   Pre calculatet values in BSD format von w1 + w2 + .. an aber normal binary abgelegten adressen
  //   akk ist jetzt bsd Darstellung 010101...
  //   contents of rom_1 (hex, n*v repeats v):
  //   0,ffffffffffffffff,ffffffffffffffff,fffffffffffffffe,1,0,0,ffffffffffffffff
  //   ,1,0,0,ffffffffffffffff,2,1,1
  //   wird jetzt BSD shifter der 01 hinten anhängt
  //   bsd adder addiert jetzt ROM abgelegent bsd wert
  //   (im wohl codierten format) mit bsd akkumulator
endmodule
