// Digital circuit TCtoBsd.dig as structural Verilog
module TCtoBsd (
  input  [3:0] inTC,
  output [7:0] outBsd
);


  assign outBsd = {inTC[3], 1'b1, inTC[2], 1'b1, inTC[1], 1'b1, inTC[0], 1'b1};
endmodule
