// Digital circuit bsdShifter.dig as structural Verilog
module bsdShifter (
  input  [17:0] in,
  output [17:0] out,
  output [1:0] carry
);


  assign carry = in[17:16];
  assign out = {in[15:0], 2'b10};
endmodule
