// Digital circuit bsdToBin.dig as structural Verilog
module bsdToBin (
  input  [17:0] in,
  output [9:0] out,
  output carry
);

  wire or_1_out, or_2_out, or_3_out, or_4_out, or_5_out, or_6_out, or_7_out, or_8_out, or_9_out;
  wire [8:0] and_1_out, not_1_out;

  and and_1 (and_1_out[0], in[0], in[1]);
  or or_1 (or_1_out, in[0], in[1]);
  and and_2 (and_1_out[1], in[2], in[3]);
  or or_2 (or_2_out, in[2], in[3]);
  and and_3 (and_1_out[2], in[4], in[5]);
  or or_3 (or_3_out, in[4], in[5]);
  and and_4 (and_1_out[3], in[6], in[7]);
  or or_4 (or_4_out, in[6], in[7]);
  and and_5 (and_1_out[4], in[8], in[9]);
  or or_5 (or_5_out, in[8], in[9]);
  and and_6 (and_1_out[5], in[10], in[11]);
  or or_6 (or_6_out, in[10], in[11]);
  and and_7 (and_1_out[6], in[12], in[13]);
  or or_7 (or_7_out, in[12], in[13]);
  and and_8 (and_1_out[7], in[14], in[15]);
  or or_8 (or_8_out, in[14], in[15]);
  and and_9 (and_1_out[8], in[16], in[17]);
  or or_9 (or_9_out, in[16], in[17]);
  not not_1 (not_1_out[0], or_1_out);
  not not_2 (not_1_out[1], or_2_out);
  not not_3 (not_1_out[2], or_3_out);
  not not_4 (not_1_out[3], or_4_out);
  not not_5 (not_1_out[4], or_5_out);
  not not_6 (not_1_out[5], or_6_out);
  not not_7 (not_1_out[6], or_7_out);
  not not_8 (not_1_out[7], or_8_out);
  not not_9 (not_1_out[8], or_9_out);
  Sub #(.Bits(10)) sub_1 (.a({1'b0, and_1_out}), .b({1'b0, not_1_out}), .c_i(1'b0), .s(out), .c_o(carry));
endmodule
