// Digital circuit bsdToBin4B.dig as structural Verilog
module bsdToBin4B (
  input  [9:0] in,
  output [5:0] out,
  output carry
);

  wire or_1_out, or_2_out, or_3_out, or_4_out, or_5_out;
  wire [4:0] and_5_out, not_5_out;

  and and_1 (and_5_out[0], in[0], in[1]);
  or or_1 (or_1_out, in[0], in[1]);
  and and_2 (and_5_out[1], in[2], in[3]);
  or or_2 (or_2_out, in[2], in[3]);
  and and_3 (and_5_out[2], in[4], in[5]);
  or or_3 (or_3_out, in[4], in[5]);
  and and_4 (and_5_out[3], in[6], in[7]);
  or or_4 (or_4_out, in[6], in[7]);
  and and_5 (and_5_out[4], in[8], in[9]);
  or or_5 (or_5_out, in[8], in[9]);
  not not_1 (not_5_out[0], or_1_out);
  not not_2 (not_5_out[1], or_2_out);
  not not_3 (not_5_out[2], or_3_out);
  not not_4 (not_5_out[3], or_4_out);
  not not_5 (not_5_out[4], or_5_out);
  Sub #(.Bits(6)) sub_1 (.a({1'b0, and_5_out}), .b({1'b0, not_5_out}), .c_i(1'b0), .s(out), .c_o(carry));
endmodule
