// Digital circuit 4bBsdTCAdder.dig as structural Verilog
module _4bBsdTCAdder (
  input  [3:0] inTC,
  input  [7:0] inBSD,
  output [9:0] bsdOut
);

  Add add_1 (.a(inBSD[6]), .b(inBSD[7]), .c_i(inTC[3]), .s(bsdOut[7]), .c_o(bsdOut[8]));
  not not_1 (bsdOut[9], inTC[3]);
  Add add_2 (.a(inBSD[4]), .b(inBSD[5]), .c_i(inTC[2]), .s(bsdOut[5]), .c_o(bsdOut[6]));
  Add add_3 (.a(inBSD[2]), .b(inBSD[3]), .c_i(inTC[1]), .s(bsdOut[3]), .c_o(bsdOut[4]));
  Add add_4 (.a(inBSD[0]), .b(inBSD[1]), .c_i(inTC[0]), .s(bsdOut[1]), .c_o(bsdOut[2]));

  assign bsdOut[0] = 1'b0;
endmodule
