// Digital circuit TheAdder.dig as structural Verilog
module TheAdder (
  input  [7:0] \input ,
  input  [7:0] uio,
  input  clk,
  input  rst,
  output [7:0] outBSD
);

  wire and_1_out, and_2_out, not_1_out, or_1_out, or_2_out, or_3_out;
  wire [1:0] register_3_q_2;
  wire [3:0] multiplexer_1_out, register_1_q;
  wire [7:0] register_2_q, register_3_q;
  wire [7:4] multiplexer_1_out_2;
  wire [9:0] _4bbsdtcadder_1_bsdout, multiplexer_2_out;

  Multiplexer #(.Bits(8)) multiplexer_1 (
    .sel(rst), .in_0(\input ), .in_1({8{1'b0}}), .out({multiplexer_1_out_2, multiplexer_1_out}));
  not not_1 (not_1_out, uio[0]);
  and and_1 (and_1_out, not_1_out, uio[1]);
  and and_2 (and_2_out, uio[0], uio[1]);
  or or_1 (or_1_out, and_1_out, rst);
  or or_2 (or_2_out, and_2_out, rst);
  Register #(.Bits(4)) register_1 (.D(multiplexer_1_out), .C(clk), .en(or_1_out), .Q(register_1_q));
  Register #(.Bits(8)) register_2 (
    .D({multiplexer_1_out_2, multiplexer_1_out}), .C(clk), .en(or_2_out), .Q(register_2_q));
  _4bBsdTCAdder _4bbsdtcadder_1 (.inTC(register_1_q), .inBSD(register_2_q), .bsdOut(_4bbsdtcadder_1_bsdout));
  Multiplexer #(.Bits(10)) multiplexer_2 (
    .sel(rst), .in_0(_4bbsdtcadder_1_bsdout), .in_1({10{1'b0}}), .out(multiplexer_2_out));
  or or_3 (or_3_out, uio[2], rst);
  Register #(.Bits(10)) register_3 (.D(multiplexer_2_out), .C(clk), .en(or_3_out), .Q({register_3_q_2, register_3_q}));
  Multiplexer #(.Bits(8)) multiplexer_3 (
    .sel(uio[3]), .in_0(register_3_q), .in_1({{6{1'b0}}, register_3_q_2}), .out(outBSD));

  // Notes on the sheet:
  //   uio: tiny tapeout uio[7:0] GPIO
  //   Funktionsweise:
  //   input kann selected werden über select reg uio[0]
  //   uio[1] lädt an entsprechen sel gesettes register den input wert
  //   nach addition kann über ouput load die jeweiligen bsd bits an outut gelegt werden
  //   ouput sel selektiert hier wegen 10 bit aber 8 bit output entweder die stellen 0-7 oder 8-9
  //   reset schreibt 0 in alle register im nächsten takt
  //   data in
  //   tiny tapeout ui_in[7:0]
  //   select reg
  //   load
  //   output load
  //   output sel
  //   [-8,7]
  //   4 bit Twos complement
  //   [-15 . 15]
  //   4 digit BSD
  //   8 pyhsical bit
endmodule
